// Logisim project 2^nmod5.circ as structural Verilog: 4 circuits, main circuit main
module main (
);

  mod5 mod5_1 ();  // open: in_1, out_2, out_3, out_4, out_5, out_6
endmodule

module nextStateLogic (
  input  s0,
  input  s1,
  input  in,
  output ss0,
  output ss1
);

  wire and_1_out, and_2_out, and_3_out, and_4_out, and_5_out, and_6_out, not_1_out, not_2_out, not_3_out,
       not_4_out, not_5_out, not_6_out, not_7_out, not_8_out;

  not not_1 (not_1_out, s0);
  not not_2 (not_2_out, s1);
  not not_3 (not_3_out, s0);
  not not_4 (not_4_out, s1);
  not not_5 (not_5_out, s0);
  not not_6 (not_6_out, in);
  not not_7 (not_7_out, s1);
  not not_8 (not_8_out, in);
  and and_1 (and_1_out, not_1_out, s1);
  and and_2 (and_2_out, s0, not_2_out);
  and and_3 (and_3_out, not_3_out, not_4_out, in);
  and and_4 (and_4_out, not_5_out, s1, not_6_out);
  and and_5 (and_5_out, s0, not_7_out, not_8_out);
  and and_6 (and_6_out, s0, s1, in);
  or or_1 (ss0, and_1_out, and_2_out);
  or or_2 (ss1, and_3_out, and_4_out, and_5_out, and_6_out);
endmodule

module \output  (
  input  s0,
  input  s1,
  input  in,
  output o0,
  output o1,
  output o2,
  output o3,
  output o4
);

  wire and_1_out, and_2_out, and_3_out, and_4_out, and_5_out, and_6_out, and_7_out, and_8_out, and_9_out,
       and_10_out, and_11_out, and_12_out, and_13_out, and_14_out, and_15_out, and_16_out, not_1_out,
       not_2_out, not_3_out, not_4_out, not_5_out, not_6_out, not_7_out, not_8_out, not_9_out, not_10_out,
       not_11_out, not_12_out;

  not not_1 (not_1_out, s0);
  not not_2 (not_2_out, s1);
  not not_3 (not_3_out, s0);
  not not_4 (not_4_out, s1);
  not not_5 (not_5_out, s0);
  not not_6 (not_6_out, s1);
  not not_7 (not_7_out, s0);
  not not_8 (not_8_out, s1);
  and and_1 (and_1_out, not_1_out, not_2_out);
  not not_9 (not_9_out, in);
  and and_2 (and_2_out, s0, s1);
  not not_10 (not_10_out, in);
  and and_3 (and_3_out, not_3_out, not_4_out);
  and and_4 (and_4_out, s0, s1);
  and and_5 (and_5_out, not_5_out, s1);
  and and_6 (and_6_out, s0, not_6_out);
  and and_7 (and_7_out, not_7_out, s1);
  not not_11 (not_11_out, in);
  and and_8 (and_8_out, s0, not_8_out);
  not not_12 (not_12_out, in);
  and and_9 (and_9_out, and_1_out, not_9_out);
  and and_10 (and_10_out, and_2_out, not_10_out);
  and and_11 (and_11_out, and_3_out, in);
  and and_12 (and_12_out, and_4_out, in);
  and and_13 (and_13_out, and_5_out, in);
  and and_14 (and_14_out, and_6_out, in);
  and and_15 (and_15_out, and_7_out, not_11_out);
  and and_16 (and_16_out, and_8_out, not_12_out);
  or or_1 (o1, and_9_out, and_10_out);
  or or_2 (o2, and_11_out, and_12_out);
  or or_3 (o3, and_13_out, and_14_out);
  or or_4 (o4, and_15_out, and_16_out);

  assign o0 = 1'b0;
endmodule

module mod5 (
  input  in_1,
  output out_2,
  output out_3,
  output out_4,
  output out_5,
  output out_6
);

  wire clock_1_out;
  wire [1:0] nextstatelogic_1_ss0, register_1_q;

  nextStateLogic nextstatelogic_1 (
    .s0(register_1_q[0]), .s1(register_1_q[1]), .in(in_1), .ss0(nextstatelogic_1_ss0[0]),
    .ss1(nextstatelogic_1_ss0[1]));
  Register #(.width(2)) register_1 (.D(nextstatelogic_1_ss0), .Q(register_1_q), .clk(clock_1_out));  // open: en, clr
  Clock clock_1 (.out(clock_1_out));
  \output  output_1 (
    .s0(register_1_q[0]), .s1(register_1_q[1]), .in(in_1), .o0(out_2), .o1(out_3), .o2(out_4), .o3(out_5),
    .o4(out_6));
endmodule
