// Logisim project P0_L0_CRC.circ as structural Verilog: 2 circuits, main circuit CRC
module CRC (
  input  [7:0] A,
  input  [3:0] B,
  output [10:0] out_3
);

  wire [0:0] shifter_1_out_3, shifter_1_out_4, shifter_1_out_5;
  wire [3:0] n4_bit_sub_1_out_3, n4_bit_sub_2_out_3, n4_bit_sub_3_out_3, n4_bit_sub_5_out_3,
       n4_bit_sub_6_out_3, n4_bit_sub_7_out_3, shifter_1_out_2;
  wire [3:3] n4_bit_sub_4_out_3, n4_bit_sub_8_out_3;
  wire [10:0] bit_extender_1_out;
  wire [10:4] shifter_1_out;

  assign bit_extender_1_out = {{3{1'b0}}, A};  // Bit_Extender bit_extender_1
  Shifter #(.width(11)) shifter_1 (
    .in(bit_extender_1_out), .\dist (4'b0011),
    .out({shifter_1_out, shifter_1_out_2[0], shifter_1_out_3[0], shifter_1_out_4[0], shifter_1_out_5[0]}));
  _4_bit_sub u_4_bit_sub_1 (.\被除数 (shifter_1_out[10:7]), .out_3(n4_bit_sub_1_out_3), .\除数 (B));
  _4_bit_sub u_4_bit_sub_2 (.\被除数 ({n4_bit_sub_1_out_3[2:0], shifter_1_out[6]}), .out_3(n4_bit_sub_2_out_3), .\除数 (B));
  _4_bit_sub u_4_bit_sub_3 (.\被除数 ({n4_bit_sub_2_out_3[2:0], shifter_1_out[5]}), .out_3(n4_bit_sub_3_out_3), .\除数 (B));
  _4_bit_sub u_4_bit_sub_4 (
    .\被除数 ({n4_bit_sub_3_out_3[2:0], shifter_1_out[4]}),
    .out_3({n4_bit_sub_4_out_3[3], shifter_1_out_2[3:1]}), .\除数 (B));
  _4_bit_sub u_4_bit_sub_5 (.\被除数 (shifter_1_out_2), .out_3(n4_bit_sub_5_out_3), .\除数 (B));
  _4_bit_sub u_4_bit_sub_6 (
    .\被除数 ({n4_bit_sub_5_out_3[2:0], shifter_1_out_3[0]}), .out_3(n4_bit_sub_6_out_3), .\除数 (B));
  _4_bit_sub u_4_bit_sub_7 (
    .\被除数 ({n4_bit_sub_6_out_3[2:0], shifter_1_out_4[0]}), .out_3(n4_bit_sub_7_out_3), .\除数 (B));
  _4_bit_sub u_4_bit_sub_8 (
    .\被除数 ({n4_bit_sub_7_out_3[2:0], shifter_1_out_5[0]}), .out_3({n4_bit_sub_8_out_3[3], out_3[2:0]}),
    .\除数 (B));

  assign out_3[10:3] = A;
endmodule

module _4_bit_sub (
  input  [3:0] \除数 ,
  input  [3:0] \被除数 ,
  output [3:0] out_3
);

  wire comparator_1_eq;
  wire [3:0] xor_1_out;

  Comparator #(.width(1)) comparator_1 (.a(1'b0), .b(\被除数 [3]), .eq(comparator_1_eq));  // open: gt, lt
  assign xor_1_out = \被除数  ^ \除数 ;  // XOR_Gate xor_1, 4 bits wide
  Multiplexer #(.width(4)) multiplexer_1 (
    .in0(xor_1_out), .in1(\被除数 ), .out(out_3), .sel(comparator_1_eq));  // open: en
endmodule
