// Logisim project P0_L0_FSM.circ as structural Verilog: 3 circuits, main circuit fsm
module fsm (
  input  reset,
  input  [1:0] \input ,
  output out_3
);

  wire clk;
  wire [1:0] cur_sta, multiplexer_1_out, nxt_statae_1_st0s;

  Clock u_clk (.out(clk));
  nxt_statae nxt_statae_1 (
    .in0(\input [0]), .st0s(nxt_statae_1_st0s[0]), .in1(\input [1]), .st0(cur_sta[0]), .st1(cur_sta[1]),
    .st1s(nxt_statae_1_st0s[1]));
  Multiplexer #(.width(2)) multiplexer_1 (
    .in0(nxt_statae_1_st0s), .in1(2'b00), .out(multiplexer_1_out), .sel(reset));  // open: en
  Register #(.width(2)) register_1 (.D(multiplexer_1_out), .Q(cur_sta), .clk(clk));  // open: en, clr
  out out_1 (.in0(\input [0]), .\output (out_3), .in1(\input [1]), .s0(cur_sta[0]), .s1(cur_sta[1]));
endmodule

module nxt_statae (
  input  in0,
  input  in1,
  input  st0,
  input  st1,
  output st0s,
  output st1s
);

  wire and_1_out, and_2_out, and_3_out, not_1_out, not_2_out, not_3_out, not_4_out, not_5_out, or_1_out;

  not not_1 (not_1_out, in1);
  not not_2 (not_2_out, st0);
  not not_3 (not_3_out, st1);
  and and_1 (and_1_out, not_3_out, st0);
  not not_4 (not_4_out, st1);
  and and_2 (and_2_out, not_4_out, st0);
  not not_5 (not_5_out, in0);
  and and_3 (and_3_out, not_1_out, in0);
  or or_1 (or_1_out, not_2_out, and_1_out);
  and and_4 (st1s, and_2_out, not_5_out);
  and and_5 (st0s, and_3_out, or_1_out);
endmodule

module out (
  input  in0,
  input  in1,
  input  s0,
  input  s1,
  output \output 
);

  wire and_1_out, not_1_out, not_2_out;

  and and_1 (and_1_out, s1, not_1_out);
  not not_1 (not_1_out, s0);
  not not_2 (not_2_out, in0);
  and and_2 (\output , and_1_out, not_2_out);
endmodule
