// Logisim project P0_L0_GRF.circ as structural Verilog: 1 circuit, main circuit grf
module grf (
  input  in_1,
  input  reset,
  input  WE,
  input  [4:0] A1,
  input  [4:0] A2,
  input  [4:0] A3,
  input  [31:0] WD,
  output [31:0] out1,
  output [31:0] out2
);

  wire _0, _1, _2, _3, _4, _5, _6, _7, _8, _9, _10, _11, _12, _13, _14, _15, _16, _17, _18, _19, _20, _21,
       _22, _23, _24, _25, _26, _27, _28, _29, _30, _31, and_1_out, and_2_out, and_3_out, and_4_out,
       and_5_out, and_6_out, and_7_out, and_8_out, and_9_out, and_10_out, and_11_out, and_12_out, and_13_out,
       and_14_out, and_15_out, and_16_out, and_17_out, and_18_out, and_19_out, and_20_out, and_21_out,
       and_22_out, and_23_out, and_24_out, and_25_out, and_26_out, and_27_out, and_28_out, and_29_out,
       and_30_out, and_31_out, and_32_out;
  wire [31:0] o0, o1, o2, o3, o4, o5, o6, o7, o8, o9, o10, o11, o12, o13, o14, o15, o16, o17, o18, o19, o20,
       o21, o22, o23, o24, o25, o26, o27, o28, o29, o30, o31;

  and and_1 (and_1_out, _16, WE);
  and and_2 (and_2_out, _21, WE);
  and and_3 (and_3_out, _25, WE);
  Decoder #(.select(5)) decoder_1 (
    .out0(_0), .out1(_1), .out2(_2), .out3(_3), .out4(_4), .out5(_5), .out6(_6), .out7(_7), .out8(_8),
    .out9(_9), .out10(_10), .out11(_11), .out12(_12), .out13(_13), .out14(_14), .out15(_15), .out16(_16),
    .out17(_17), .out18(_18), .out19(_19), .out20(_20), .out21(_21), .out22(_22), .out23(_23), .out24(_24),
    .out25(_25), .out26(_26), .out27(_27), .out28(_28), .out29(_29), .out30(_30), .out31(_31), .sel(A3));  // open: en
  and and_4 (and_4_out, _12, WE);
  and and_5 (and_5_out, _14, WE);
  and and_6 (and_6_out, _18, WE);
  and and_7 (and_7_out, _29, WE);
  Register #(.width(32)) register_1 (.D(WD), .en(and_4_out), .Q(o12), .clk(in_1), .clr(reset));
  Register #(.width(32)) register_2 (.D(WD), .en(and_5_out), .Q(o14), .clk(in_1), .clr(reset));
  Register #(.width(32)) register_3 (.D(WD), .en(and_1_out), .Q(o16), .clk(in_1), .clr(reset));
  Register #(.width(32)) register_4 (.D(WD), .en(and_6_out), .Q(o18), .clk(in_1), .clr(reset));
  Register #(.width(32)) register_5 (.D(WD), .en(and_2_out), .Q(o21), .clk(in_1), .clr(reset));
  Register #(.width(32)) register_6 (.D(WD), .en(and_3_out), .Q(o25), .clk(in_1), .clr(reset));
  Register #(.width(32)) register_7 (.D(WD), .en(and_7_out), .Q(o29), .clk(in_1), .clr(reset));
  and and_8 (and_8_out, _13, WE);
  and and_9 (and_9_out, _15, WE);
  and and_10 (and_10_out, _17, WE);
  and and_11 (and_11_out, _19, WE);
  and and_12 (and_12_out, _22, WE);
  and and_13 (and_13_out, _26, WE);
  and and_14 (and_14_out, _30, WE);
  and and_15 (and_15_out, _1, WE);
  and and_16 (and_16_out, _3, WE);
  Register #(.width(32)) register_8 (.D(WD), .en(and_12_out), .Q(o22), .clk(in_1), .clr(reset));
  Register #(.width(32)) register_9 (.D(WD), .en(and_13_out), .Q(o26), .clk(in_1), .clr(reset));
  Register #(.width(32)) register_10 (.D(WD), .en(and_15_out), .Q(o1), .clk(in_1), .clr(reset));
  Register #(.width(32)) register_11 (.D(WD), .en(and_16_out), .Q(o3), .clk(in_1), .clr(reset));
  and and_17 (and_17_out, _5, WE);
  Register #(.width(32)) register_12 (.D(WD), .en(and_8_out), .Q(o13), .clk(in_1), .clr(reset));
  Register #(.width(32)) register_13 (.D(WD), .en(and_9_out), .Q(o15), .clk(in_1), .clr(reset));
  Register #(.width(32)) register_14 (.D(WD), .en(and_10_out), .Q(o17), .clk(in_1), .clr(reset));
  Register #(.width(32)) register_15 (.D(WD), .en(and_11_out), .Q(o19), .clk(in_1), .clr(reset));
  Register #(.width(32)) register_16 (.D(WD), .en(and_14_out), .Q(o30), .clk(in_1), .clr(reset));
  and and_18 (and_18_out, _27, WE);
  Register #(.width(32)) register_17 (.D(WD), .en(and_17_out), .Q(o5), .clk(in_1), .clr(reset));
  and and_19 (and_19_out, _20, WE);
  and and_20 (and_20_out, _23, WE);
  and and_21 (and_21_out, _31, WE);
  and and_22 (and_22_out, _2, WE);
  and and_23 (and_23_out, _4, WE);
  Register #(.width(32)) register_18 (.D(WD), .en(and_20_out), .Q(o23), .clk(in_1), .clr(reset));
  Register #(.width(32)) register_19 (.D(WD), .en(and_18_out), .Q(o27), .clk(in_1), .clr(reset));
  Register #(.width(32)) register_20 (.D(WD), .en(and_21_out), .Q(o31), .clk(in_1), .clr(reset));
  Register #(.width(32)) register_21 (.D(WD), .en(and_22_out), .Q(o2), .clk(in_1), .clr(reset));
  Register #(.width(32)) register_22 (.D(WD), .en(and_23_out), .Q(o4), .clk(in_1), .clr(reset));
  and and_24 (and_24_out, _6, WE);
  and and_25 (and_25_out, _7, WE);
  and and_26 (and_26_out, _8, WE);
  and and_27 (and_27_out, _9, WE);
  and and_28 (and_28_out, _10, WE);
  and and_29 (and_29_out, _11, WE);
  Register #(.width(32)) register_23 (.D(WD), .en(and_19_out), .Q(o20), .clk(in_1), .clr(reset));
  Register #(.width(32)) register_24 (.D(WD), .en(and_24_out), .Q(o6), .clk(in_1), .clr(reset));
  Register #(.width(32)) register_25 (.D(WD), .en(and_25_out), .Q(o7), .clk(in_1), .clr(reset));
  Register #(.width(32)) register_26 (.D(WD), .en(and_26_out), .Q(o8), .clk(in_1), .clr(reset));
  Register #(.width(32)) register_27 (.D(WD), .en(and_27_out), .Q(o9), .clk(in_1), .clr(reset));
  Register #(.width(32)) register_28 (.D(WD), .en(and_28_out), .Q(o10), .clk(in_1), .clr(reset));
  Register #(.width(32)) register_29 (.D(WD), .en(and_29_out), .Q(o11), .clk(in_1), .clr(reset));
  and and_30 (and_30_out, _24, WE);
  and and_31 (and_31_out, _28, WE);
  and and_32 (and_32_out, _0, WE);
  Register #(.width(32)) register_30 (.D(WD), .en(and_30_out), .Q(o24), .clk(in_1), .clr(reset));
  Register #(.width(32)) register_31 (.D(WD), .en(and_31_out), .Q(o28), .clk(in_1), .clr(reset));
  Register #(.width(32)) register_32 (.D({32{1'b0}}), .en(and_32_out), .Q(o0), .clk(in_1), .clr(reset));
  Multiplexer #(.select(5), .width(32)) multiplexer_1 (
    .in0(o0), .in1(o1), .in2(o2), .in3(o3), .in4(o4), .in5(o5), .in6(o6), .in7(o7), .in8(o8), .in9(o9),
    .in10(o10), .in11(o11), .in12(o12), .in13(o13), .in14(o14), .in15(o15), .in16(o16), .in17(o17),
    .in18(o18), .in19(o19), .in20(o20), .in21(o21), .in22(o22), .in23(o23), .in24(o24), .in25(o25),
    .in26(o26), .in27(o27), .in28(o28), .in29(o29), .in30(o30), .in31(o31), .out(out1), .sel(A1));  // open: en
  Multiplexer #(.select(5), .width(32)) multiplexer_2 (
    .in0(o0), .in1(o1), .in2(o2), .in3(o3), .in4(o4), .in5(o5), .in6(o6), .in7(o7), .in8(o8), .in9(o9),
    .in10(o10), .in11(o11), .in12(o12), .in13(o13), .in14(o14), .in15(o15), .in16(o16), .in17(o17),
    .in18(o18), .in19(o19), .in20(o20), .in21(o21), .in22(o22), .in23(o23), .in24(o24), .in25(o25),
    .in26(o26), .in27(o27), .in28(o28), .in29(o29), .in30(o30), .in31(o31), .out(out2), .sel(A2));  // open: en

  // Other names for the same wires on the sheet: clk = in_1
endmodule
