// Logisim project P0_L1_ftoi.circ as structural Verilog: 1 circuit, main circuit ftoi
// s
module ftoi (
  input  [15:0] in_1,
  output [31:0] out_2
);

  wire comparator_1_gt;
  wire [4:0] bit_extender_4_out;
  wire [5:0] bit_extender_2_out, bit_extender_5_out, subtractor_1_out;
  wire [10:0] bit_extender_1_out;
  wire [31:0] adder_1_out, bit_extender_3_out, not_1_out, shifter_1_out, shifter_2_out, \signed ;

  assign bit_extender_1_out = {{1{1'b1}}, in_1[9:0]};  // Bit_Extender bit_extender_1
  assign bit_extender_2_out = {{1{1'b0}}, in_1[14:10]};  // Bit_Extender bit_extender_2
  assign bit_extender_3_out = {{21{1'b0}}, bit_extender_1_out};  // Bit_Extender bit_extender_3
  Subtractor #(.width(6)) subtractor_1 (
    .a(bit_extender_2_out), .b(6'b001111), .out(subtractor_1_out));  // open: bin, bout
  Bit_Extender #(.in_width(6), .out_width(5)) bit_extender_4 (.in(subtractor_1_out), .out(bit_extender_4_out));
  Shifter #(.width(32)) shifter_1 (.in(bit_extender_3_out), .\dist (bit_extender_4_out), .out(shifter_1_out));
  Shifter #(.width(32), .shift("lr")) shifter_2 (.in(shifter_1_out), .\dist (5'b01010), .out(shifter_2_out));
  assign not_1_out = ~shifter_2_out;  // NOT_Gate not_1, 32 bits wide
  Adder #(.width(32)) adder_1 (.a(not_1_out), .b(32'h1), .out(adder_1_out));  // open: cin, cout
  Multiplexer #(.width(32)) multiplexer_1 (
    .in0(shifter_2_out), .in1(adder_1_out), .out(\signed ), .sel(in_1[15]));  // open: en
  Comparator #(.width(6)) comparator_1 (.a(6'b001111), .b(bit_extender_5_out), .gt(comparator_1_gt));  // open: eq, lt
  assign bit_extender_5_out = {{1{1'b0}}, in_1[14:10]};  // Bit_Extender bit_extender_5
  Multiplexer #(.width(32)) multiplexer_2 (
    .in0(\signed ), .in1({32{1'b0}}), .out(out_2), .sel(comparator_1_gt));  // open: en

  // Other names for the same wires on the sheet: exponent[4:0] = in_1[14:10]; frac[9:0] = in_1[9:0]; S = in_1[15]
endmodule
