// Logisim project adder算补码不用考虑进位P0上机.circ as structural Verilog: 3 circuits, main circuit main
module main (
  input  [1:0] S,
  input  [1:0] T1,
  input  [1:0] T2,
  input  [1:0] T3,
  output out_5
);

  wire comparator_1_eq, comparator_2_lt;
  wire [3:0] adder_1_out, adder_2_out, adder_3_out, s_judge_1_out0, t_judge_1_out0, t_judge_2_out0,
       t_judge_3_out0;

  T_JUDGE t_judge_1 (
    .S1(T1[1]), .OUT3(t_judge_1_out0[3]), .S0(T1[0]), .OUT2(t_judge_1_out0[2]), .OUT1(t_judge_1_out0[1]),
    .OUT0(t_judge_1_out0[0]));
  T_JUDGE t_judge_2 (
    .S1(T2[1]), .OUT3(t_judge_2_out0[3]), .S0(T2[0]), .OUT2(t_judge_2_out0[2]), .OUT1(t_judge_2_out0[1]),
    .OUT0(t_judge_2_out0[0]));
  T_JUDGE t_judge_3 (
    .S1(T3[1]), .OUT3(t_judge_3_out0[3]), .S0(T3[0]), .OUT2(t_judge_3_out0[2]), .OUT1(t_judge_3_out0[1]),
    .OUT0(t_judge_3_out0[0]));
  s_JUDGE s_judge_1 (
    .S1(S[1]), .OUT3(s_judge_1_out0[3]), .S0(S[0]), .OU2(s_judge_1_out0[2]), .OUT1(s_judge_1_out0[1]),
    .OUT0(s_judge_1_out0[0]));
  Comparator #(.width(2), .mode("unsigned")) comparator_1 (.a(S), .b(2'b11), .eq(comparator_1_eq));  // open: gt, lt
  Adder #(.width(4)) adder_1 (.a(s_judge_1_out0), .b(t_judge_1_out0), .out(adder_1_out));  // open: cin, cout
  Adder #(.width(4)) adder_2 (.a(adder_1_out), .b(t_judge_2_out0), .out(adder_2_out));  // open: cin, cout
  Adder #(.width(4)) adder_3 (.a(adder_2_out), .b(t_judge_3_out0), .out(adder_3_out));  // open: cin, cout
  Comparator #(.width(4)) comparator_2 (.a(4'b0000), .b(adder_3_out), .lt(comparator_2_lt));  // open: gt, eq
  or or_1 (out_5, comparator_1_eq, comparator_2_lt);
endmodule

module s_JUDGE (
  input  S1,
  input  S0,
  output OUT3,
  output OU2,
  output OUT1,
  output OUT0
);

  wire nand_1_out;

  nand nand_1 (nand_1_out, S0, S0);
  nand nand_2 (OUT0, S1, nand_1_out);

  assign OU2 = S0;
  assign OUT1 = S0;
  assign OUT3 = S0;
endmodule

module T_JUDGE (
  input  S1,
  input  S0,
  output OUT3,
  output OUT2,
  output OUT1,
  output OUT0
);

  wire nand_1_out;

  nand nand_1 (nand_1_out, S0, S0);
  nand nand_2 (OUT0, S1, nand_1_out);

  assign OUT1 = S0;
  assign OUT2 = S0;
  assign OUT3 = S0;
endmodule
