// Logisim project fibonacci.circ as structural Verilog: 3 circuits, main circuit main
// 1
module main (
  input  [2:0] in_1,
  output [3:0] out_2
);

  wire \计数_1_control信号 ;
  wire [3:0] \计算_1_out_3 ;

  \计数  \u_计数_1  (.\输入 (in_1), .\复位 (1'b0), .\control信号 (\计数_1_control信号 ));
  \计算  \u_计算_1  (.\复位 (1'b0), .\控制信号 (\计数_1_control信号 ), .out_3(\计算_1_out_3 ));
  Multiplexer #(.width(4)) multiplexer_1 (
    .in0(4'b0000), .in1(\计算_1_out_3 ), .out(out_2), .sel(\计数_1_control信号 ));  // open: en
endmodule

module \计数  (
  input  [2:0] \输入 ,
  input  \复位 ,
  output \control信号 
);

  wire clk;
  wire [3:0] bit_extender_1_out, counter_1_q;

  Clock clock_1 (.out(clk));
  assign bit_extender_1_out = {{1{1'b0}}, \输入 };  // Bit_Extender bit_extender_1
  Counter #(.width(4), .max('hf), .ongoal("stay")) counter_1 (
    .Q(counter_1_q), .clk(clk), .clr(\复位 ));  // open: load, D, count, carry
  Comparator #(.width(4), .mode("unsigned")) comparator_1 (
    .a(bit_extender_1_out), .b(counter_1_q), .lt(\control信号 ));  // open: gt, eq

  // Other names for the same wires on the sheet: input[2:0] = \输入 ; reset = \复位 
endmodule

module \计算  (
  input  \复位 ,
  input  \控制信号 ,
  output [3:0] out_3
);

  wire clk, control, init;
  wire [3:0] adder_1_out, multiplexer_1_out, pre;

  Clock clock_1 (.out(clk));
  Counter #(.width(1), .max('h1), .ongoal("stay")) counter_1 (
    .Q(init), .clk(clk), .clr(\复位 ));  // open: load, D, count, carry
  not not_1 (control, \控制信号 );
  Multiplexer #(.width(4)) multiplexer_1 (.in0(4'b0001), .in1(out_3), .out(multiplexer_1_out), .sel(init));  // open: en
  Register #(.width(4)) u_pre (.D(multiplexer_1_out), .en(control), .Q(pre), .clk(clk), .clr(\复位 ));
  Adder #(.width(4)) adder_1 (.a(pre), .b(out_3), .out(adder_1_out));  // open: cin, cout
  Register #(.width(4)) now (.D(adder_1_out), .en(control), .Q(out_3), .clk(clk), .clr(\复位 ));

  // Other names for the same wires on the sheet: now[3:0] = out_3; reset = \复位 
endmodule
