// Logisim project fibonacci2.0.circ as structural Verilog: 6 circuits, main circuit main
module main (
  input  [31:0] in_1,
  output [31:0] out_2
);

  wire freeze, n_low;

  \计数逻辑  \u_计数逻辑_1  (.\复位 (1'b0), .\输入 (in_1), .\n的最低位 (n_low), .freeze(freeze));
  \计算逻辑  \u_计算逻辑_1  (.\循环结束标志 (freeze), .\当前数的最低位 (n_low), .\复位 (1'b0), .out_4(out_2));

  // Other names for the same wires on the sheet: in[31:0] = in_1; out[31:0] = out_2
endmodule

module \矩阵存储  (
  input  in_1,
  input  \复位 ,
  input  \使能 ,
  input  [31:0] in_4,
  input  [31:0] in_5,
  input  [31:0] in_6,
  input  [31:0] in_7,
  output [31:0] out_8,
  output [31:0] out_9,
  output [31:0] out_10,
  output [31:0] o11
);

  Register #(.width(32)) register_1 (.D(in_4), .en(\使能 ), .Q(out_8), .clk(in_1), .clr(\复位 ));
  Register #(.width(32)) register_2 (.D(in_6), .en(\使能 ), .Q(out_10), .clk(in_1), .clr(\复位 ));
  Register #(.width(32)) register_3 (.D(in_5), .en(\使能 ), .Q(out_9), .clk(in_1), .clr(\复位 ));
  Register #(.width(32)) register_4 (.D(in_7), .en(\使能 ), .Q(o11), .clk(in_1), .clr(\复位 ));

  // Other names for the same wires on the sheet: _00[31:0] = in_4; _01[31:0] = in_5; _10[31:0] = in_6;
  //   _11[31:0] = in_7; clk = in_1; enable = \使能 ; o00[31:0] = out_8; o01[31:0] = out_9; o10[31:0] = out_10;
  //   reset = \复位 

  // Notes on the sheet:
  //   用于存储矩阵，6个输入，1个使能，4个数和一个复位
endmodule

module \矩阵乘法  (
  input  [31:0] in_1,
  input  [31:0] in_2,
  input  [31:0] in_3,
  input  [31:0] in_4,
  input  [31:0] in_5,
  input  [31:0] in_6,
  input  [31:0] in_7,
  input  [31:0] in_8,
  output [31:0] out_9,
  output [31:0] out_10,
  output [31:0] out_11,
  output [31:0] out_12
);

  wire [31:0] multiplier_1_out, multiplier_2_out, multiplier_3_out, multiplier_4_out, multiplier_5_out,
       multiplier_6_out, multiplier_7_out, multiplier_8_out;

  Multiplier #(.width(32)) multiplier_1 (.a(in_1), .b(in_4), .out(multiplier_1_out));  // open: cin, cout
  Multiplier #(.width(32)) multiplier_2 (.a(in_3), .b(in_8), .out(multiplier_2_out));  // open: cin, cout
  Multiplier #(.width(32)) multiplier_3 (.a(in_5), .b(in_2), .out(multiplier_3_out));  // open: cin, cout
  Multiplier #(.width(32)) multiplier_4 (.a(in_7), .b(in_6), .out(multiplier_4_out));  // open: cin, cout
  Multiplier #(.width(32)) multiplier_5 (.a(in_7), .b(in_8), .out(multiplier_5_out));  // open: cin, cout
  Multiplier #(.width(32)) multiplier_6 (.a(in_4), .b(in_5), .out(multiplier_6_out));  // open: cin, cout
  Multiplier #(.width(32)) multiplier_7 (.a(in_1), .b(in_2), .out(multiplier_7_out));  // open: cin, cout
  Multiplier #(.width(32)) multiplier_8 (.a(in_3), .b(in_6), .out(multiplier_8_out));  // open: cin, cout
  Adder #(.width(32)) adder_1 (.a(multiplier_1_out), .b(multiplier_2_out), .out(out_10));  // open: cin, cout
  Adder #(.width(32)) adder_2 (.a(multiplier_3_out), .b(multiplier_4_out), .out(out_11));  // open: cin, cout
  Adder #(.width(32)) adder_3 (.a(multiplier_5_out), .b(multiplier_6_out), .out(out_12));  // open: cin, cout
  Adder #(.width(32)) adder_4 (.a(multiplier_7_out), .b(multiplier_8_out), .out(out_9));  // open: cin, cout

  // Other names for the same wires on the sheet: _00[31:0] = in_1; _00_[31:0] = in_2; _01[31:0] = in_3;
  //   _01_[31:0] = in_4; _10[31:0] = in_5; _10_[31:0] = in_6; _11[31:0] = in_7; _11_[31:0] = in_8; o00[31:0] = out_9;
  //   o01[31:0] = out_10; o10[31:0] = out_11; o11[31:0] = out_12
endmodule

module \矩阵MUX  (
  input  [31:0] in_1,
  input  [31:0] in_2,
  input  [31:0] in_3,
  input  [31:0] in_4,
  input  [31:0] in_5,
  input  [31:0] in_6,
  input  [31:0] in_7,
  input  [31:0] in_8,
  input  sel,
  output [31:0] out_10,
  output [31:0] out_11,
  output [31:0] out_12,
  output [31:0] out_13
);

  Multiplexer #(.width(32)) multiplexer_1 (.in0(in_1), .in1(in_2), .out(out_10), .sel(sel));  // open: en
  Multiplexer #(.width(32)) multiplexer_2 (.in0(in_3), .in1(in_4), .out(out_11), .sel(sel));  // open: en
  Multiplexer #(.width(32)) multiplexer_3 (.in0(in_5), .in1(in_6), .out(out_12), .sel(sel));  // open: en
  Multiplexer #(.width(32)) multiplexer_4 (.in0(in_7), .in1(in_8), .out(out_13), .sel(sel));  // open: en

  // Other names for the same wires on the sheet: _00[31:0] = in_1; _00_[31:0] = in_2; _01[31:0] = in_3;
  //   _01_[31:0] = in_4; _10[31:0] = in_5; _10_[31:0] = in_6; _11[31:0] = in_7; _11_[31:0] = in_8; o00[31:0] = out_10;
  //   o01[31:0] = out_11; o10[31:0] = out_12; o11[31:0] = out_13
endmodule

module \计算逻辑  (
  input  \循环结束标志 ,
  input  \当前数的最低位 ,
  input  \复位 ,
  output [31:0] out_4
);

  wire clk, enable, init;
  wire [31:0] a1, a2, a3, a4, s1, s2, s3, s4, \矩阵mux_1_out_10 , \矩阵mux_1_out_11 , \矩阵mux_1_out_12 ,
       \矩阵mux_1_out_13 , \矩阵mux_2_out_10 , \矩阵mux_2_out_11 , \矩阵mux_2_out_12 , \矩阵mux_2_out_13 ,
       \矩阵mux_3_out_10 , \矩阵mux_3_out_11 , \矩阵mux_3_out_12 , \矩阵mux_3_out_13 , \矩阵乘法_1_out_9 ,
       \矩阵乘法_1_out_10 , \矩阵乘法_1_out_11 , \矩阵乘法_1_out_12 , \矩阵乘法_2_out_9 , \矩阵乘法_2_out_10 , \矩阵乘法_2_out_11 ,
       \矩阵乘法_2_out_12 ;

  Clock clock_1 (.out(clk));
  not not_1 (enable, \循环结束标志 );
  Counter #(.width(1), .max('h1), .ongoal("stay")) counter_1 (
    .Q(init), .clk(clk), .clr(\复位 ));  // open: load, D, count, carry
  \矩阵MUX  \u_矩阵mux_1  (
    .in_1(32'h1), .in_2(a1), .in_3({32{1'b0}}), .in_4(a2), .in_5({32{1'b0}}), .in_6(a3), .in_7(32'h1),
    .in_8(a4), .sel(\当前数的最低位 ), .out_10(\矩阵mux_1_out_10 ), .out_11(\矩阵mux_1_out_11 ),
    .out_12(\矩阵mux_1_out_12 ), .out_13(\矩阵mux_1_out_13 ));
  \矩阵乘法  \u_矩阵乘法_1  (
    .in_1(a1), .in_2(a1), .in_3(a2), .in_4(a2), .in_5(a3), .in_6(a3), .in_7(a4), .in_8(a4),
    .out_9(\矩阵乘法_1_out_9 ), .out_10(\矩阵乘法_1_out_10 ), .out_11(\矩阵乘法_1_out_11 ), .out_12(\矩阵乘法_1_out_12 ));
  \矩阵乘法  \u_矩阵乘法_2  (
    .in_1(s1), .in_2(\矩阵mux_1_out_10 ), .in_3(s2), .in_4(\矩阵mux_1_out_11 ), .in_5(s3),
    .in_6(\矩阵mux_1_out_12 ), .in_7(s4), .in_8(\矩阵mux_1_out_13 ), .out_9(\矩阵乘法_2_out_9 ),
    .out_10(\矩阵乘法_2_out_10 ), .out_11(\矩阵乘法_2_out_11 ), .out_12(\矩阵乘法_2_out_12 ));
  \矩阵MUX  \u_矩阵mux_2  (
    .in_1(32'h1), .in_2(\矩阵乘法_1_out_9 ), .in_3(32'h1), .in_4(\矩阵乘法_1_out_10 ), .in_5(32'h1),
    .in_6(\矩阵乘法_1_out_11 ), .in_7({32{1'b0}}), .in_8(\矩阵乘法_1_out_12 ), .sel(init), .out_10(\矩阵mux_2_out_10 ),
    .out_11(\矩阵mux_2_out_11 ), .out_12(\矩阵mux_2_out_12 ), .out_13(\矩阵mux_2_out_13 ));
  Multiplexer #(.width(32)) multiplexer_1 (.in0(s2), .in1({32{1'b0}}), .out(out_4), .sel(enable));  // open: en
  \矩阵存储  \u_矩阵存储_1  (
    .\复位 (\复位 ), .in_4(\矩阵mux_2_out_10 ), .in_5(\矩阵mux_2_out_11 ), .in_6(\矩阵mux_2_out_12 ),
    .in_7(\矩阵mux_2_out_13 ), .out_8(a1), .out_9(a2), .out_10(a3), .o11(a4), .\使能 (enable), .in_1(clk));
  \矩阵MUX  \u_矩阵mux_3  (
    .in_1(32'h1), .in_2(\矩阵乘法_2_out_9 ), .in_3({32{1'b0}}), .in_4(\矩阵乘法_2_out_10 ), .in_5({32{1'b0}}),
    .in_6(\矩阵乘法_2_out_11 ), .in_7(32'h1), .in_8(\矩阵乘法_2_out_12 ), .sel(init), .out_10(\矩阵mux_3_out_10 ),
    .out_11(\矩阵mux_3_out_11 ), .out_12(\矩阵mux_3_out_12 ), .out_13(\矩阵mux_3_out_13 ));
  \矩阵存储  \u_矩阵存储_2  (
    .\复位 (\复位 ), .in_4(\矩阵mux_3_out_10 ), .in_5(\矩阵mux_3_out_11 ), .in_6(\矩阵mux_3_out_12 ),
    .in_7(\矩阵mux_3_out_13 ), .out_8(s1), .out_9(s2), .out_10(s3), .o11(s4), .\使能 (enable), .in_1(clk));

  // Other names for the same wires on the sheet: freeze = \循环结束标志 ; judge = \当前数的最低位 ; reset = \复位 
endmodule

module \计数逻辑  (
  input  \复位 ,
  input  [31:0] \输入 ,
  output \n的最低位 ,
  output freeze
);

  wire clk, cnt, comparator_1_eq;
  wire [31:0] multiplexer_1_out, n, shifter_1_out;

  Clock clock_1 (.out(clk));
  Counter #(.width(1), .max('h1), .ongoal("stay")) counter_1 (
    .Q(cnt), .clk(clk), .clr(\复位 ));  // open: load, D, count, carry
  Shifter #(.width(32), .shift("lr")) shifter_1 (.in(n), .\dist (5'b00001), .out(shifter_1_out));
  Bit_Extender #(.in_width(32), .out_width(1)) bit_extender_1 (.in(n), .out(\n的最低位 ));
  Multiplexer #(.width(32)) multiplexer_1 (
    .in0(\输入 ), .in1(shifter_1_out), .out(multiplexer_1_out), .sel(cnt));  // open: en
  Comparator #(.width(32), .mode("unsigned")) comparator_1 (
    .a(n), .b({32{1'b0}}), .eq(comparator_1_eq));  // open: gt, lt
  Register #(.width(32)) register_1 (.D(multiplexer_1_out), .Q(n), .clk(clk), .clr(\复位 ));  // open: en
  Multiplexer multiplexer_2 (.in0(1'b0), .in1(comparator_1_eq), .out(freeze), .sel(cnt));  // open: en

  // Other names for the same wires on the sheet: input[31:0] = \输入 ; reset = \复位 

  // Notes on the sheet:
  //   注意：n在第1个上升沿之前的初值要初始化为零，在比较时，对第一个时钟沿之前的情况要保证在这个阶段freeze为0，不能为1
endmodule
