// Logisim project match1101.circ as structural Verilog: 1 circuit, main circuit main
module main (
  input  in_1,
  output out_2
);

  wire clock_1_out, not_1_out, not_2_out, register_1_q, register_2_q, register_3_q, register_4_q;

  Clock clock_1 (.out(clock_1_out));
  not not_1 (not_1_out, in_1);
  Register #(.width(1)) register_1 (.D(not_1_out), .Q(register_1_q), .clk(clock_1_out));  // open: en, clr
  Register #(.width(1)) register_2 (.D(register_1_q), .Q(register_2_q), .clk(clock_1_out));  // open: en, clr
  not not_2 (not_2_out, register_2_q);
  Register #(.width(1)) register_3 (.D(register_2_q), .Q(register_3_q), .clk(clock_1_out));  // open: en, clr
  Register #(.width(1)) register_4 (.D(register_3_q), .Q(register_4_q), .clk(clock_1_out));  // open: en, clr
  and and_1 (out_2, register_4_q, register_3_q, not_2_out, register_1_q);

  // Notes on the sheet:
  //   可重叠
  //   不可重叠
endmodule
