// Logisim project myfibonacci.circ as structural Verilog: 8 circuits, main circuit main
module main (
  input  [31:0] \input ,
  output [31:0] out_2
);

  wire freeze, n_low;

  \计数逻辑  \u_计数逻辑_1  (.\input (\input ), .clr(1'b0), .freeze(freeze), .n_low(n_low));
  \计算逻辑  \u_计算逻辑_1  (.n_low(n_low), .freeze(freeze), .clr(1'b0), .out_4(out_2));
endmodule

module \矩阵存储  (
  input  clk,
  input  clr,
  input  ena,
  input  [31:0] in_4,
  input  [31:0] in_5,
  input  [31:0] in_6,
  input  [31:0] in_7,
  output [31:0] out_8,
  output [31:0] out_9,
  output [31:0] out_10,
  output [31:0] out_11
);

  Register #(.width(32)) register_1 (.D(in_4), .en(ena), .Q(out_8), .clk(clk), .clr(clr));
  Register #(.width(32)) register_2 (.D(in_6), .en(ena), .Q(out_10), .clk(clk), .clr(clr));
  Register #(.width(32)) register_3 (.D(in_5), .en(ena), .Q(out_9), .clk(clk), .clr(clr));
  Register #(.width(32)) register_4 (.D(in_7), .en(ena), .Q(out_11), .clk(clk), .clr(clr));

  // Other names for the same wires on the sheet: _11[31:0] = out_8; _12[31:0] = out_9; _21[31:0] = out_10;
  //   _22[31:0] = out_11; a11[31:0] = in_4; a12[31:0] = in_5; a21[31:0] = in_6; a22[31:0] = in_7
endmodule

module \矩阵乘法  (
  input  [31:0] a11,
  input  [31:0] a12,
  input  [31:0] a21,
  input  [31:0] a22,
  input  [31:0] b11,
  input  [31:0] b12,
  input  [31:0] b21,
  input  [31:0] b22,
  output [31:0] c11,
  output [31:0] c12,
  output [31:0] c21,
  output [31:0] c22
);

  wire [31:0] multiplier_1_out, multiplier_2_out, multiplier_3_out, multiplier_4_out, multiplier_5_out,
       multiplier_6_out, multiplier_7_out, multiplier_8_out;

  Multiplier #(.width(32)) multiplier_1 (.a(a11), .b(b11), .out(multiplier_1_out));  // open: cin, cout
  Multiplier #(.width(32)) multiplier_2 (.a(a12), .b(b21), .out(multiplier_2_out));  // open: cin, cout
  Multiplier #(.width(32)) multiplier_3 (.a(a11), .b(b12), .out(multiplier_3_out));  // open: cin, cout
  Multiplier #(.width(32)) multiplier_4 (.a(a12), .b(b22), .out(multiplier_4_out));  // open: cin, cout
  Multiplier #(.width(32)) multiplier_5 (.a(a21), .b(b11), .out(multiplier_5_out));  // open: cin, cout
  Multiplier #(.width(32)) multiplier_6 (.a(a22), .b(b21), .out(multiplier_6_out));  // open: cin, cout
  Multiplier #(.width(32)) multiplier_7 (.a(a21), .b(b12), .out(multiplier_7_out));  // open: cin, cout
  Multiplier #(.width(32)) multiplier_8 (.a(a22), .b(b22), .out(multiplier_8_out));  // open: cin, cout
  Adder #(.width(32)) adder_1 (.a(multiplier_1_out), .b(multiplier_2_out), .out(c11));  // open: cin, cout
  Adder #(.width(32)) adder_2 (.a(multiplier_3_out), .b(multiplier_4_out), .out(c12));  // open: cin, cout
  Adder #(.width(32)) adder_3 (.a(multiplier_5_out), .b(multiplier_6_out), .out(c21));  // open: cin, cout
  Adder #(.width(32)) adder_4 (.a(multiplier_7_out), .b(multiplier_8_out), .out(c22));  // open: cin, cout
endmodule

module \矩阵MUX  (
  input  [31:0] a11,
  input  [31:0] a12,
  input  [31:0] a21,
  input  [31:0] a22,
  input  [31:0] b11,
  input  [31:0] b12,
  input  [31:0] b21,
  input  [31:0] b22,
  input  sel,
  output [31:0] c11,
  output [31:0] c12,
  output [31:0] c21,
  output [31:0] c22
);

  Multiplexer #(.width(32)) multiplexer_1 (.in0(a11), .in1(b11), .out(c11), .sel(sel));  // open: en
  Multiplexer #(.width(32)) multiplexer_2 (.in0(a12), .in1(b12), .out(c12), .sel(sel));  // open: en
  Multiplexer #(.width(32)) multiplexer_3 (.in0(a21), .in1(b21), .out(c21), .sel(sel));  // open: en
  Multiplexer #(.width(32)) multiplexer_4 (.in0(a22), .in1(b22), .out(c22), .sel(sel));  // open: en
endmodule

module \计算逻辑  (
  input  n_low,
  input  freeze,
  input  clr,
  output [31:0] out_4
);

  wire clk, ena, init;
  wire [31:0] a11, a12, a21, a22, s11, s12, s21, s22, \初始矩阵_1_out_1 , \初始矩阵_1_out_2 , \初始矩阵_1_out_3 ,
       \初始矩阵_1_out_4 , \单位阵_1_out_1 , \单位阵_1_out_2 , \单位阵_1_out_3 , \单位阵_1_out_4 , \单位阵_2_out_1 ,
       \单位阵_2_out_2 , \单位阵_2_out_3 , \单位阵_2_out_4 , \矩阵mux_1_c11 , \矩阵mux_1_c12 , \矩阵mux_1_c21 ,
       \矩阵mux_1_c22 , \矩阵mux_2_c11 , \矩阵mux_2_c12 , \矩阵mux_2_c21 , \矩阵mux_2_c22 , \矩阵mux_3_c11 ,
       \矩阵mux_3_c12 , \矩阵mux_3_c21 , \矩阵mux_3_c22 , \矩阵乘法_1_c11 , \矩阵乘法_1_c12 , \矩阵乘法_1_c21 , \矩阵乘法_1_c22 ,
       \矩阵乘法_2_c11 , \矩阵乘法_2_c12 , \矩阵乘法_2_c21 , \矩阵乘法_2_c22 ;

  Clock u_clk (.out(clk));
  Counter #(.width(1), .max('h1), .ongoal("stay")) u_init (
    .Q(init), .clk(clk), .clr(clr));  // open: load, D, count, carry
  \单位阵  \u_单位阵_1  (.out_1(\单位阵_1_out_1 ), .out_2(\单位阵_1_out_2 ), .out_3(\单位阵_1_out_3 ), .out_4(\单位阵_1_out_4 ));
  \矩阵乘法  \u_矩阵乘法_1  (
    .a11(a11), .a12(a12), .c11(\矩阵乘法_1_c11 ), .a21(a21), .a22(a22), .c12(\矩阵乘法_1_c12 ), .b11(a11), .b12(a12),
    .c21(\矩阵乘法_1_c21 ), .b21(a21), .b22(a22), .c22(\矩阵乘法_1_c22 ));
  not not_1 (ena, freeze);
  \矩阵乘法  \u_矩阵乘法_2  (
    .a11(s11), .a12(s12), .c11(\矩阵乘法_2_c11 ), .a21(s21), .a22(s22), .c12(\矩阵乘法_2_c12 ), .b11(\矩阵mux_1_c11 ),
    .b12(\矩阵mux_1_c12 ), .c21(\矩阵乘法_2_c21 ), .b21(\矩阵mux_1_c21 ), .b22(\矩阵mux_1_c22 ), .c22(\矩阵乘法_2_c22 ));
  \矩阵MUX  \u_矩阵mux_1  (
    .a11(\单位阵_1_out_1 ), .a12(\单位阵_1_out_2 ), .c11(\矩阵mux_1_c11 ), .a21(\单位阵_1_out_3 ), .a22(\单位阵_1_out_4 ),
    .c12(\矩阵mux_1_c12 ), .b11(a11), .b12(a12), .c21(\矩阵mux_1_c21 ), .b21(a21), .b22(a22),
    .c22(\矩阵mux_1_c22 ), .sel(n_low));
  \初始矩阵  \u_初始矩阵_1  (.out_1(\初始矩阵_1_out_1 ), .out_2(\初始矩阵_1_out_2 ), .out_3(\初始矩阵_1_out_3 ), .out_4(\初始矩阵_1_out_4 ));
  \单位阵  \u_单位阵_2  (.out_1(\单位阵_2_out_1 ), .out_2(\单位阵_2_out_2 ), .out_3(\单位阵_2_out_3 ), .out_4(\单位阵_2_out_4 ));
  \矩阵MUX  \u_矩阵mux_2  (
    .a11(\初始矩阵_1_out_1 ), .a12(\初始矩阵_1_out_2 ), .c11(\矩阵mux_2_c11 ), .a21(\初始矩阵_1_out_3 ),
    .a22(\初始矩阵_1_out_4 ), .c12(\矩阵mux_2_c12 ), .b11(\矩阵乘法_1_c11 ), .b12(\矩阵乘法_1_c12 ), .c21(\矩阵mux_2_c21 ),
    .b21(\矩阵乘法_1_c21 ), .b22(\矩阵乘法_1_c22 ), .c22(\矩阵mux_2_c22 ), .sel(init));
  Multiplexer #(.width(32)) multiplexer_1 (.in0({32{1'b0}}), .in1(s12), .out(out_4), .sel(freeze));  // open: en
  \矩阵MUX  \u_矩阵mux_3  (
    .a11(\单位阵_2_out_1 ), .a12(\单位阵_2_out_2 ), .c11(\矩阵mux_3_c11 ), .a21(\单位阵_2_out_3 ), .a22(\单位阵_2_out_4 ),
    .c12(\矩阵mux_3_c12 ), .b11(\矩阵乘法_2_c11 ), .b12(\矩阵乘法_2_c12 ), .c21(\矩阵mux_3_c21 ), .b21(\矩阵乘法_2_c21 ),
    .b22(\矩阵乘法_2_c22 ), .c22(\矩阵mux_3_c22 ), .sel(init));
  \矩阵存储  \u_矩阵存储_1  (
    .clk(clk), .clr(clr), .ena(ena), .in_4(\矩阵mux_2_c11 ), .in_5(\矩阵mux_2_c12 ), .in_6(\矩阵mux_2_c21 ),
    .in_7(\矩阵mux_2_c22 ), .out_8(a11), .out_9(a12), .out_10(a21), .out_11(a22));
  \矩阵存储  \u_矩阵存储_2  (
    .clk(clk), .clr(clr), .ena(ena), .in_4(\矩阵mux_3_c11 ), .in_5(\矩阵mux_3_c12 ), .in_6(\矩阵mux_3_c21 ),
    .in_7(\矩阵mux_3_c22 ), .out_8(s11), .out_9(s12), .out_10(s21), .out_11(s22));
endmodule

module \计数逻辑  (
  input  [31:0] \input ,
  input  clr,
  output freeze,
  output n_low
);

  wire clk, comparator_1_eq, init;
  wire [31:0] multiplexer_1_out, n, shifter_1_out;

  Counter #(.width(1), .max('h1), .ongoal("stay")) counter_1 (
    .Q(init), .clk(clk), .clr(clr));  // open: load, D, count, carry
  Clock u_clk (.out(clk));
  Shifter #(.width(32), .shift("lr")) shifter_1 (.in(n), .\dist (5'b00001), .out(shifter_1_out));
  Comparator #(.width(32)) comparator_1 (.a({32{1'b0}}), .b(n), .eq(comparator_1_eq));  // open: gt, lt
  Multiplexer #(.width(32)) multiplexer_1 (
    .in0(\input ), .in1(shifter_1_out), .out(multiplexer_1_out), .sel(init));  // open: en
  Multiplexer multiplexer_2 (.in0(1'b0), .in1(comparator_1_eq), .out(freeze), .sel(init));  // open: en
  Bit_Extender #(.in_width(32), .out_width(1)) bit_extender_1 (.in(n), .out(n_low));
  Register #(.width(32)) register_1 (.D(multiplexer_1_out), .Q(n), .clk(clk), .clr(clr));  // open: en
endmodule

module \初始矩阵  (
  output [31:0] out_1,
  output [31:0] out_2,
  output [31:0] out_3,
  output [31:0] out_4
);


  assign out_1 = 32'h1;
  assign out_2 = 32'h1;
  assign out_3 = 32'h1;
  assign out_4 = {32{1'b0}};
endmodule

module \单位阵  (
  output [31:0] out_1,
  output [31:0] out_2,
  output [31:0] out_3,
  output [31:0] out_4
);


  assign out_1 = 32'h1;
  assign out_2 = {32{1'b0}};
  assign out_3 = {32{1'b0}};
  assign out_4 = 32'h1;
endmodule
