// Logisim project swapAndSort.circ as structural Verilog: 4 circuits, main circuit main
module main (
);

  _4bit_sort u_4bit_sort_1 ();  // open: in_1, in_2, in_3, in_4, out_5, out_6, out_7, out_8
endmodule

module _1bit_swap (
  input  i1,
  input  i2,
  input  s,
  output o1,
  output o2
);

  wire and_1_out, and_2_out, and_3_out, and_4_out, and_5_out, and_6_out, and_7_out, and_8_out, n1, n2, ns;

  not not_1 (n1, i1);
  not not_2 (n2, i2);
  not not_3 (ns, s);
  and and_1 (and_1_out, i1, n2, ns);
  and and_2 (and_2_out, i1, i2, ns);
  and and_3 (and_3_out, n1, i2, s);
  and and_4 (and_4_out, i1, i2, s);
  and and_5 (and_5_out, n1, i2, ns);
  and and_6 (and_6_out, i1, i2, ns);
  and and_7 (and_7_out, i1, n2, s);
  and and_8 (and_8_out, i1, i2, s);
  or or_1 (o1, and_1_out, and_2_out, and_3_out, and_4_out);
  or or_2 (o2, and_5_out, and_6_out, and_7_out, and_8_out);

  // Other names for the same wires on the sheet: _1 = i1; _2 = i2
endmodule

module _4bit_swap (
  input  [3:0] n1,
  input  [3:0] n2,
  input  \是否交换 ,
  output [3:0] out_4,
  output [3:0] out_5
);

  _1bit_swap u_1bit_swap_1 (.i1(n1[0]), .i2(n2[0]), .s(\是否交换 ), .o1(out_4[0]), .o2(out_5[0]));
  _1bit_swap u_1bit_swap_2 (.i1(n1[1]), .i2(n2[1]), .s(\是否交换 ), .o1(out_4[1]), .o2(out_5[1]));
  _1bit_swap u_1bit_swap_3 (.i1(n1[3]), .i2(n2[3]), .s(\是否交换 ), .o1(out_4[3]), .o2(out_5[3]));
  _1bit_swap u_1bit_swap_4 (.i1(n1[2]), .i2(n2[2]), .s(\是否交换 ), .o1(out_4[2]), .o2(out_5[2]));
endmodule

module _4bit_sort (
  input  [3:0] in_1,
  input  [3:0] in_2,
  input  [3:0] in_3,
  input  [3:0] in_4,
  output [3:0] out_5,
  output [3:0] out_6,
  output [3:0] out_7,
  output [3:0] out_8
);

  wire comparator_1_gt, comparator_2_gt, comparator_3_gt, comparator_4_gt, comparator_5_gt;
  wire [3:0] n4bit_swap_1_out_4, n4bit_swap_1_out_5, n4bit_swap_2_out_4, n4bit_swap_2_out_5,
       n4bit_swap_3_out_5, n4bit_swap_4_out_4;

  Comparator #(.width(4), .mode("unsigned")) comparator_1 (.a(in_1), .b(in_2), .gt(comparator_1_gt));  // open: eq, lt
  Comparator #(.width(4), .mode("unsigned")) comparator_2 (.a(in_3), .b(in_4), .gt(comparator_2_gt));  // open: eq, lt
  _4bit_swap u_4bit_swap_1 (
    .n1(in_1), .n2(in_2), .\是否交换 (comparator_1_gt), .out_4(n4bit_swap_1_out_4), .out_5(n4bit_swap_1_out_5));
  _4bit_swap u_4bit_swap_2 (
    .n1(in_3), .n2(in_4), .\是否交换 (comparator_2_gt), .out_4(n4bit_swap_2_out_4), .out_5(n4bit_swap_2_out_5));
  Comparator #(.width(4), .mode("unsigned")) comparator_3 (
    .a(n4bit_swap_1_out_4), .b(n4bit_swap_2_out_4), .gt(comparator_3_gt));  // open: eq, lt
  Comparator #(.width(4), .mode("unsigned")) comparator_4 (
    .a(n4bit_swap_1_out_5), .b(n4bit_swap_2_out_5), .gt(comparator_4_gt));  // open: eq, lt
  _4bit_swap u_4bit_swap_3 (
    .n1(n4bit_swap_1_out_4), .n2(n4bit_swap_2_out_4), .\是否交换 (comparator_3_gt), .out_4(out_5),
    .out_5(n4bit_swap_3_out_5));
  _4bit_swap u_4bit_swap_4 (
    .n1(n4bit_swap_1_out_5), .n2(n4bit_swap_2_out_5), .\是否交换 (comparator_4_gt), .out_4(n4bit_swap_4_out_4),
    .out_5(out_8));
  Comparator #(.width(4), .mode("unsigned")) comparator_5 (
    .a(n4bit_swap_3_out_5), .b(n4bit_swap_4_out_4), .gt(comparator_5_gt));  // open: eq, lt
  _4bit_swap u_4bit_swap_5 (
    .n1(n4bit_swap_3_out_5), .n2(n4bit_swap_4_out_4), .\是否交换 (comparator_5_gt), .out_4(out_6), .out_5(out_7));
endmodule
