// Logisim project test01.circ as structural Verilog: 2 circuits, main circuit main
module main (
  input  [5:0] in_1,
  output [2:0] out_2
);

  wire [2:0] xor_1_out;

  assign out_2 = ~xor_1_out;  // NOT_Gate not_1, 3 bits wide
  assign xor_1_out = in_1[2:0] ^ in_1[5:3];  // XOR_Gate xor_1, 3 bits wide
endmodule

// 我的加法器
module myAdder (
  input  cin,
  input  \输入a ,
  input  \输入B ,
  output cout,
  output res
);

  wire and_1_out, and_2_out, xor_2_out;

  or or_1 (cout, and_1_out, and_2_out);
  and and_1 (and_1_out, cin, xor_2_out);
  and and_2 (and_2_out, \输入B , \输入a );
  xor xor_1 (res, cin, xor_2_out);
  xor xor_2 (xor_2_out, \输入a , \输入B );

  // Notes on the sheet:
  //   cout=ab + cin(a^b)
endmodule
