// Logisim project vote.circ as structural Verilog: 5 circuits, main circuit main
module main (
  input  [1:0] S,
  input  [1:0] T0,
  input  [1:0] T1,
  input  [1:0] T2,
  output RES
);

  wire comparator_1_eq, comparator_2_gt;
  wire [2:0] bitadder_1_out, bitadder_2_out;
  wire [3:0] agree_2_x, bit_extender_1_out, bit_extender_2_out, judge_disagree_1_x;

  judge_t agree (.s1(S[1]), .s0(S[0]), .x(agree_2_x[3]));
  J_S_DIS j_s_dis_1 (.S1(S[1]), .S0(S[0]), .x(judge_disagree_1_x[3]));
  judge_t agree_2 (.s1(T0[1]), .s0(T0[0]), .x(agree_2_x[0]));
  judge_disagree judge_disagree_1 (.s1(T0[1]), .s0(T0[0]), .x(judge_disagree_1_x[0]));
  judge_t agree_3 (.s1(T1[1]), .s0(T1[0]), .x(agree_2_x[1]));
  judge_disagree judge_disagree_2 (.s1(T1[1]), .s0(T1[0]), .x(judge_disagree_1_x[1]));
  judge_t agree_4 (.s1(T2[1]), .s0(T2[0]), .x(agree_2_x[2]));
  judge_disagree judge_disagree_3 (.s1(T2[1]), .s0(T2[0]), .x(judge_disagree_1_x[2]));
  Comparator #(.width(2)) comparator_1 (.a(S), .b(2'b11), .eq(comparator_1_eq));  // open: gt, lt
  or or_1 (RES, comparator_1_eq, comparator_2_gt);
  BitAdder #(.width(4)) bitadder_1 (.in0(agree_2_x), .out(bitadder_1_out));
  BitAdder #(.width(4)) bitadder_2 (.in0(judge_disagree_1_x), .out(bitadder_2_out));
  assign bit_extender_1_out = {{1{1'b0}}, bitadder_1_out};  // Bit_Extender bit_extender_1
  assign bit_extender_2_out = {{1{1'b0}}, bitadder_2_out};  // Bit_Extender bit_extender_2
  Comparator #(.width(4)) comparator_2 (
    .a(bit_extender_1_out), .b(bit_extender_2_out), .gt(comparator_2_gt));  // open: eq, lt

  // Notes on the sheet:
  //   disagree
  //   disagree
  //   disagree
endmodule

module judge_t (
  input  s1,
  input  s0,
  output x
);

  wire nand_1_out, nand_2_out, nand_3_out;

  nand nand_1 (nand_1_out, s1, s1);
  nand nand_2 (nand_2_out, s0, s0);
  nand nand_3 (nand_3_out, nand_1_out, nand_2_out);
  nand nand_4 (x, nand_3_out, nand_3_out);
endmodule

module judge_disagree (
  input  s1,
  input  s0,
  output x
);


  assign x = s0;
endmodule

module jud_S_agree (
  input  S1,
  input  S0,
  output out_3
);
endmodule

module J_S_DIS (
  input  S1,
  input  S0,
  output x
);

  wire nand_1_out, nand_2_out;

  nand nand_1 (nand_1_out, S1, S1);
  nand nand_2 (nand_2_out, nand_1_out, S0);
  nand nand_3 (x, nand_2_out, nand_2_out);
endmodule
