// Logisim project P3_L0_CPU.circ as structural Verilog: 8 circuits, main circuit main
module main (
  input  RESET,
  output [31:0] instru,
  output RegWrite,
  output [4:0] RegAddr,
  output [31:0] RegData,
  output MemWrite,
  output [4:0] MemAddr,
  output [31:0] MemData
);

  wire BSEL, CLK, ZERO;
  wire [1:0] BORH, EXTOP, WDSEL, WRSEL;
  wire [2:0] ALUOP, NPCOP;
  wire [31:0] ALUC, DMOUT, ext_1_ext, multiplexer_3_out, PC4, PC_DI, PC_DO, RD1, RD2;

  Clock u_CLK (.out(CLK));
  Register #(.width(32)) PC (.D(PC_DI), .Q(PC_DO), .clk(CLK), .clr(RESET));  // open: en
  NPC npc_1 (.PC(PC_DO), .IMM(instru[25:0]), .RA(RD1), .NPCOP(NPCOP), .ZERO(ZERO), .NPC(PC_DI), .PC4(PC4));
  Multiplexer #(.select(2), .width(5)) multiplexer_1 (
    .in0(instru[20:16]), .in1(instru[15:11]), .in2({5{1'b1}}), .out(RegAddr), .sel(WRSEL));  // open: in3, en
  Multiplexer #(.select(2), .width(32)) multiplexer_2 (
    .in0({ALUC[31:7], MemAddr, ALUC[1:0]}), .in1(DMOUT), .in2(PC4), .out(RegData), .sel(WDSEL));  // open: in3, en
  ROM #(.addrWidth(5), .dataWidth(32)) rom_1 (.addr(PC_DO[6:2]), .data(instru));  // open: sel
  GRF grf_1 (
    .RFWr(RegWrite), .A1(instru[25:21]), .A2(instru[20:16]), .A3(RegAddr), .WD(RegData), .RD1(RD1),
    .RD2(RD2), .CLK(CLK), .RESET(RESET));
  CTRL ctrl_1 (
    .FUNC(instru[5:0]), .OPCODE(instru[31:26]), .ALUOP(ALUOP), .NPCOP(NPCOP), .M1SEL(WRSEL), .M2SEL(WDSEL),
    .EXTOP(EXTOP), .RFWR(RegWrite), .DMWR(MemWrite), .M3SEL(BSEL), .BORH(BORH));
  EXT ext_1 (.F(EXTOP), .Imm(instru[15:0]), .Ext(ext_1_ext));
  Multiplexer #(.width(32)) multiplexer_3 (
    .in0(RD2), .in1(ext_1_ext), .out(multiplexer_3_out), .sel(BSEL));  // open: en
  ALU alu_1 (
    .A(RD1), .B(multiplexer_3_out), .ALUOP(ALUOP), .C({ALUC[31:7], MemAddr, ALUC[1:0]}), .ZERO(ZERO),
    .shamt(instru[10:6]));
  // Probe on RegAddr
  // Probe on RegData
  // Probe on MemAddr
  // Probe on MemData
  DM dm_1 (
    .A({ALUC[31:7], MemAddr, ALUC[1:0]}), .WD(RD2), .WR(MemWrite), .CLK(CLK), .RESET(RESET), .RD(DMOUT),
    .BORH(BORH), .out_8(MemData));

  // Other names for the same wires on the sheet: ALUC[6:2] = MemAddr; DMWR = MemWrite; func[5:0] = instru[5:0];
  //   shamt[4:0] = instru[10:6]; rd[4:0] = instru[15:11]; RT[4:0] = instru[20:16]; RS[4:0] = instru[25:21];
  //   OPCODE[5:0] = instru[31:26]; RFWR = RegWrite

  // Notes on the sheet:
  //   contents of rom_1 (hex, n*v repeats v):
  //   3c04ffff 3484ffff 0 84d821 3c051234 34a55678 85d821 a5d821 d821 a4402b 1100000c 0 1084023 ad050000
  //   a1050003 a5050008 8d100000 81110004 0 85120008 11000002 c000c1e 3442000a 3508000c 8d13fff4 8114fff8
  //   8515fffc c000c1e 213b823 1017fff8 100482b 213482b
endmodule

module NPC (
  input  [31:0] PC,
  input  [25:0] IMM,
  input  [31:0] RA,
  input  [2:0] NPCOP,
  input  ZERO,
  output [31:0] NPC,
  output [31:0] PC4
);

  wire [31:0] BEQJ, bit_extender_1_out, bit_extender_2_out, multiplexer_1_out;

  Adder #(.width(32)) adder_1 (.a(PC), .b(32'h4), .out(PC4));  // open: cin, cout
  assign bit_extender_1_out = {{14{IMM[15]}}, {IMM[15:0], 2'b00}};  // Bit_Extender bit_extender_1
  Multiplexer #(.width(32)) multiplexer_1 (.in0(PC4), .in1(BEQJ), .out(multiplexer_1_out), .sel(ZERO));  // open: en
  Adder #(.width(32)) adder_2 (.a(PC4), .b(bit_extender_1_out), .out(BEQJ));  // open: cin, cout
  Multiplexer #(.select(3), .width(32)) multiplexer_2 (
    .in0(PC4), .in1(multiplexer_1_out), .in2({PC[31:28], IMM, 2'b00}), .in3(RA), .out(NPC), .sel(NPCOP));  // open: in4, in5, in6, in7, en
  Bit_Extender #(.in_width(16), .out_width(32), .\type ("sign")) bit_extender_2 (.out(bit_extender_2_out));  // open: in
  Shifter #(.width(32)) shifter_1 (.in(bit_extender_2_out), .\dist (5'b00010));  // open: out

  // Other names for the same wires on the sheet: JAL[31:2] = {PC[31:28], IMM}

  // Notes on the sheet:
  //   rs和rt的相等标志
endmodule

module GRF (
  input  CLK,
  input  RESET,
  input  RFWr,
  input  [4:0] A1,
  input  [4:0] A2,
  input  [4:0] A3,
  input  [31:0] WD,
  output [31:0] RD1,
  output [31:0] RD2
);

  wire W1, W2, W3, W4, W5, W6, W7, W8, W9, W10, W11, W12, W13, W14, W15, W16, W17, W18, W19, W20, W21, W22,
       W23, W24, W25, W26, W27, W28, W29, W30, W31;
  wire [31:0] _1, _2, _3, _4, _5, _6, _7, _8, _9, _10, _11, _12, _13, _14, _15, _16, _17, _18, _19, _20, _21,
       _22, _23, _24, _25, _26, _27, _28, _29, _30, _31;

  Register #(.width(32)) register_1 (.D(WD), .en(W2), .Q(_2), .clk(CLK), .clr(RESET));
  Register #(.width(32)) register_2 (.D(WD), .en(W3), .Q(_3), .clk(CLK), .clr(RESET));
  Register #(.width(32)) register_3 (.D(WD), .en(W4), .Q(_4), .clk(CLK), .clr(RESET));
  Register #(.width(32)) register_4 (.D(WD), .en(W5), .Q(_5), .clk(CLK), .clr(RESET));
  Register #(.width(32)) register_5 (.D(WD), .en(W6), .Q(_6), .clk(CLK), .clr(RESET));
  Register #(.width(32)) register_6 (.D(WD), .en(W7), .Q(_7), .clk(CLK), .clr(RESET));
  Register #(.width(32)) register_7 (.D(WD), .en(W8), .Q(_8), .clk(CLK), .clr(RESET));
  Register #(.width(32)) register_8 (.D(WD), .en(W9), .Q(_9), .clk(CLK), .clr(RESET));
  Register #(.width(32)) register_9 (.D(WD), .en(W10), .Q(_10), .clk(CLK), .clr(RESET));
  Register #(.width(32)) register_10 (.D(WD), .en(W11), .Q(_11), .clk(CLK), .clr(RESET));
  Register #(.width(32)) register_11 (.D(WD), .en(W12), .Q(_12), .clk(CLK), .clr(RESET));
  Register #(.width(32)) register_12 (.D(WD), .en(W13), .Q(_13), .clk(CLK), .clr(RESET));
  Register #(.width(32)) register_13 (.D(WD), .en(W14), .Q(_14), .clk(CLK), .clr(RESET));
  Register #(.width(32)) register_14 (.D(WD), .en(W15), .Q(_15), .clk(CLK), .clr(RESET));
  Register #(.width(32)) register_15 (.D(WD), .en(W16), .Q(_16), .clk(CLK), .clr(RESET));
  Register #(.width(32)) register_16 (.D(WD), .en(W17), .Q(_17), .clk(CLK), .clr(RESET));
  Register #(.width(32)) register_17 (.D(WD), .en(W18), .Q(_18), .clk(CLK), .clr(RESET));
  Register #(.width(32)) register_18 (.D(WD), .en(W19), .Q(_19), .clk(CLK), .clr(RESET));
  Register #(.width(32)) register_19 (.D(WD), .en(W20), .Q(_20), .clk(CLK), .clr(RESET));
  Register #(.width(32)) register_20 (.D(WD), .en(W1), .Q(_1), .clk(CLK), .clr(RESET));
  Demultiplexer #(.select(5)) demultiplexer_1 (
    .out1(W1), .out2(W2), .out3(W3), .out4(W4), .out5(W5), .out6(W6), .out7(W7), .out8(W8), .out9(W9),
    .out10(W10), .out11(W11), .out12(W12), .out13(W13), .out14(W14), .out15(W15), .out16(W16), .out17(W17),
    .out18(W18), .out19(W19), .out20(W20), .out21(W21), .out22(W22), .out23(W23), .out24(W24), .out25(W25),
    .out26(W26), .out27(W27), .out28(W28), .out29(W29), .out30(W30), .out31(W31), .in(RFWr), .sel(A3));  // open: out0, en
  Register #(.width(32)) register_21 (.D(WD), .en(W21), .Q(_21), .clk(CLK), .clr(RESET));
  Register #(.width(32)) register_22 (.D(WD), .en(W22), .Q(_22), .clk(CLK), .clr(RESET));
  Register #(.width(32)) register_23 (.D(WD), .en(W23), .Q(_23), .clk(CLK), .clr(RESET));
  Multiplexer #(.select(5), .width(32)) multiplexer_1 (
    .in0({32{1'b0}}), .in1(_1), .in2(_2), .in3(_3), .in4(_4), .in5(_5), .in6(_6), .in7(_7), .in8(_8),
    .in9(_9), .in10(_10), .in11(_11), .in12(_12), .in13(_13), .in14(_14), .in15(_15), .in16(_16), .in17(_17),
    .in18(_18), .in19(_19), .in20(_20), .in21(_21), .in22(_22), .in23(_23), .in24(_24), .in25(_25),
    .in26(_26), .in27(_27), .in28(_28), .in29(_29), .in30(_30), .in31(_31), .out(RD1), .sel(A1));  // open: en
  Multiplexer #(.select(5), .width(32)) multiplexer_2 (
    .in0({32{1'b0}}), .in1(_1), .in2(_2), .in3(_3), .in4(_4), .in5(_5), .in6(_6), .in7(_7), .in8(_8),
    .in9(_9), .in10(_10), .in11(_11), .in12(_12), .in13(_13), .in14(_14), .in15(_15), .in16(_16), .in17(_17),
    .in18(_18), .in19(_19), .in20(_20), .in21(_21), .in22(_22), .in23(_23), .in24(_24), .in25(_25),
    .in26(_26), .in27(_27), .in28(_28), .in29(_29), .in30(_30), .in31(_31), .out(RD2), .sel(A2));  // open: en
  Register #(.width(32)) register_24 (.D(WD), .en(W24), .Q(_24), .clk(CLK), .clr(RESET));
  // Probe on _31
  Register #(.width(32)) register_25 (.D(WD), .en(W31), .Q(_31), .clk(CLK), .clr(RESET));
  Register #(.width(32)) register_26 (.D(WD), .en(W30), .Q(_30), .clk(CLK), .clr(RESET));
  Register #(.width(32)) register_27 (.D(WD), .en(W29), .Q(_29), .clk(CLK), .clr(RESET));
  Register #(.width(32)) register_28 (.D(WD), .en(W28), .Q(_28), .clk(CLK), .clr(RESET));
  Register #(.width(32)) register_29 (.D(WD), .en(W27), .Q(_27), .clk(CLK), .clr(RESET));
  Register #(.width(32)) register_30 (.D(WD), .en(W26), .Q(_26), .clk(CLK), .clr(RESET));
  Register #(.width(32)) register_31 (.D(WD), .en(W25), .Q(_25), .clk(CLK), .clr(RESET));
endmodule

module ALU (
  input  [4:0] shamt,
  input  [31:0] A,
  input  [31:0] B,
  input  [2:0] ALUOP,
  output [31:0] C,
  output ZERO
);

  wire comparator_1_lt;
  wire [31:0] adder_1_out, bit_extender_1_out, or_1_out, shifter_1_out, subtractor_1_out;

  Adder #(.width(32)) adder_1 (.a(A), .b(B), .out(adder_1_out));  // open: cin, cout
  Subtractor #(.width(32)) subtractor_1 (.a(A), .b(B), .out(subtractor_1_out));  // open: bin, bout
  assign or_1_out = A | B;  // OR_Gate or_1, 32 bits wide
  Comparator #(.width(32), .mode("unsigned")) comparator_1 (.a(A), .b(B), .lt(comparator_1_lt));  // open: gt, eq
  assign bit_extender_1_out = {{31{1'b0}}, comparator_1_lt};  // Bit_Extender bit_extender_1
  Shifter #(.width(32)) shifter_1 (.in(B), .\dist (shamt), .out(shifter_1_out));
  Comparator #(.width(32)) comparator_2 (.a(A), .b(B), .eq(ZERO));  // open: gt, lt
  Multiplexer #(.select(3), .width(32)) multiplexer_1 (
    .in0(adder_1_out), .in1(subtractor_1_out), .in2(or_1_out), .in3(bit_extender_1_out), .in4(shifter_1_out),
    .out(C), .sel(ALUOP));  // open: in5, in6, in7, en
  // Probe on ALUOP
endmodule

module EXT (
  input  [1:0] F,
  input  [15:0] Imm,
  output [31:0] Ext
);

  wire [31:0] bit_extender_1_out, bit_extender_2_out;

  assign bit_extender_1_out = {{16{Imm[15]}}, Imm};  // Bit_Extender bit_extender_1
  assign bit_extender_2_out = {{16{1'b0}}, Imm};  // Bit_Extender bit_extender_2
  Multiplexer #(.select(2), .width(32)) multiplexer_1 (
    .in0(bit_extender_1_out), .in1(bit_extender_2_out), .in2({Imm, {16{1'b0}}}), .out(Ext), .sel(F));  // open: in3, en
  // Probe on F
endmodule

module DM (
  input  [1:0] BORH,
  input  [31:0] A,
  input  RESET,
  input  CLK,
  input  WR,
  input  [31:0] WD,
  output [31:0] RD,
  output [31:0] out_8
);

  wire decoder_1_out0, decoder_1_out1, decoder_1_out2, decoder_1_out3, decoder_2_out0, decoder_2_out1;
  wire [7:0] _0_7, _8_15, _16_23, _24_31, multiplexer_8_out;
  wire [15:0] multiplexer_9_out;
  wire [31:0] bit_extender_1_out, bit_extender_2_out, LB, LH;

  Decoder #(.select(2)) decoder_1 (
    .out0(decoder_1_out0), .out1(decoder_1_out1), .out2(decoder_1_out2), .out3(decoder_1_out3), .sel(A[1:0]));  // open: en
  Decoder decoder_2 (.out0(decoder_2_out0), .out1(decoder_2_out1), .sel(A[1]));  // open: en
  Multiplexer #(.width(8)) multiplexer_1 (.in0(_0_7), .in1(WD[7:0]), .out(LB[7:0]), .sel(decoder_1_out0));  // open: en
  Multiplexer #(.width(8)) multiplexer_2 (
    .in0(_8_15), .in1(WD[7:0]), .out(LB[15:8]), .sel(decoder_1_out1));  // open: en
  Multiplexer #(.width(8)) multiplexer_3 (
    .in0(_16_23), .in1(WD[7:0]), .out(LB[23:16]), .sel(decoder_1_out2));  // open: en
  Multiplexer #(.width(8)) multiplexer_4 (
    .in0(_24_31), .in1(WD[7:0]), .out(LB[31:24]), .sel(decoder_1_out3));  // open: en
  Multiplexer #(.select(2), .width(32)) multiplexer_5 (
    .in0(WD), .in1(LB), .in2(LH), .out(out_8), .sel(BORH));  // open: in3, en
  Multiplexer #(.width(16)) multiplexer_6 (
    .in0({_8_15, _0_7}), .in1(WD[15:0]), .out(LH[15:0]), .sel(decoder_2_out0));  // open: en
  Multiplexer #(.width(16)) multiplexer_7 (
    .in0({_24_31, _16_23}), .in1(WD[15:0]), .out(LH[31:16]), .sel(decoder_2_out1));  // open: en
  RAM #(.addrWidth(5), .dataWidth(32), .bus("separate")) ram_1 (
    .addr(A[6:2]), .din(out_8), .data({_24_31, _16_23, _8_15, _0_7}), .str(WR), .sel(1'b1), .clk(CLK),
    .clr(RESET));  // open: ld
  Multiplexer #(.select(2), .width(8)) multiplexer_8 (
    .in0(_0_7), .in1(_8_15), .in2(_16_23), .in3(_24_31), .out(multiplexer_8_out), .sel(A[1:0]));  // open: en
  assign bit_extender_1_out = {{24{multiplexer_8_out[7]}}, multiplexer_8_out};  // Bit_Extender bit_extender_1
  Multiplexer #(.width(16)) multiplexer_9 (
    .in0({_8_15, _0_7}), .in1({_24_31, _16_23}), .out(multiplexer_9_out), .sel(A[1]));  // open: en
  assign bit_extender_2_out = {{16{multiplexer_9_out[15]}}, multiplexer_9_out};  // Bit_Extender bit_extender_2
  Multiplexer #(.select(2), .width(32)) multiplexer_10 (
    .in0({_24_31, _16_23, _8_15, _0_7}), .in1(bit_extender_1_out), .in2(bit_extender_2_out), .out(RD),
    .sel(BORH));  // open: in3, en

  // Other names for the same wires on the sheet: A0_1[1:0] = A[1:0]; MemData[31:0] = out_8
endmodule

module CTRL (
  input  [5:0] FUNC,
  input  [5:0] OPCODE,
  output RFWR,
  output DMWR,
  output M3SEL,
  output [2:0] ALUOP,
  output [2:0] NPCOP,
  output [1:0] M1SEL,
  output [1:0] M2SEL,
  output [1:0] BORH,
  output [1:0] EXTOP
);

  wire ADDU, and_1_out, BEQ, JAL, JR, LB, LH, LUI, LW, NOP, not_1_out, not_2_out, not_3_out, not_4_out,
       not_5_out, not_6_out, not_7_out, not_8_out, not_9_out, not_10_out, not_11_out, not_12_out, ORI, SB,
       SH, SLTU, SUBU, SW;

  not not_1 (not_1_out, OPCODE[5]);
  not not_2 (not_2_out, OPCODE[4]);
  or or_1 (RFWR, LH, ALUOP[2], ADDU, SUBU, ORI, LW, LUI, SLTU, LB, JAL);
  not not_3 (not_3_out, OPCODE[2]);
  not not_4 (not_4_out, OPCODE[3]);
  not not_5 (not_5_out, OPCODE[0]);
  not not_6 (not_6_out, OPCODE[1]);
  or or_2 (DMWR, SB, SH, SW);
  and and_1 (and_1_out, not_5_out, not_6_out, not_3_out, not_4_out, not_2_out, not_1_out);
  and u_ORI (ORI, not_1_out, not_2_out, OPCODE[3], OPCODE[2], not_6_out, OPCODE[0]);
  and u_LW (LW, OPCODE[5], not_2_out, not_4_out, not_3_out, OPCODE[1], OPCODE[0]);
  and u_SW (SW, OPCODE[5], not_2_out, OPCODE[3], not_3_out, OPCODE[1], OPCODE[0]);
  and u_BEQ (BEQ, not_1_out, not_2_out, not_4_out, OPCODE[2], not_6_out, not_5_out);
  and u_LUI (LUI, not_1_out, not_2_out, OPCODE[3], OPCODE[2], OPCODE[1], OPCODE[0]);
  and u_JAL (JAL, not_1_out, not_2_out, not_4_out, not_3_out, OPCODE[1], OPCODE[0]);
  and u_SB (SB, OPCODE[5], not_2_out, OPCODE[3], not_3_out, not_6_out, not_5_out);
  and u_SH (SH, OPCODE[5], not_2_out, OPCODE[3], not_3_out, not_6_out, OPCODE[0]);
  and u_LB (LB, OPCODE[5], not_2_out, not_4_out, not_3_out, not_6_out, not_5_out);
  and u_LH (LH, OPCODE[5], not_2_out, not_4_out, not_3_out, not_6_out, OPCODE[0]);
  or or_3 (ALUOP[1], ORI, SLTU);
  not not_7 (not_7_out, FUNC[5]);
  or or_4 (ALUOP[0], SLTU, SUBU);
  not not_8 (not_8_out, FUNC[4]);
  not not_9 (not_9_out, FUNC[3]);
  not not_10 (not_10_out, FUNC[0]);
  not not_11 (not_11_out, FUNC[2]);
  not not_12 (not_12_out, FUNC[1]);
  or or_5 (NPCOP[1], JR, JAL);
  or or_6 (NPCOP[0], JR, BEQ);
  and u_ADDU (ADDU, FUNC[5], not_8_out, not_9_out, and_1_out, not_11_out, not_12_out, FUNC[0]);
  and u_SUBU (SUBU, FUNC[5], not_8_out, not_9_out, and_1_out, not_11_out, FUNC[1], FUNC[0]);
  and u_NOP (NOP, not_7_out, not_8_out, not_9_out, and_1_out, not_11_out, not_12_out, not_10_out);
  and u_JR (JR, not_7_out, not_8_out, FUNC[3], and_1_out, not_11_out, not_12_out, not_10_out);
  and u_SLTU (SLTU, FUNC[5], not_8_out, FUNC[3], and_1_out, not_11_out, FUNC[1], FUNC[0]);
  and SLL (ALUOP[2], not_7_out, not_8_out, not_9_out, and_1_out, not_11_out, not_12_out, not_10_out);
  buf or_7 (EXTOP[1], LUI);  // OR_Gate
  buf EXTOP0 (EXTOP[0], ORI);  // OR_Gate
  buf M1SEL1 (M1SEL[1], JAL);  // OR_Gate
  or M1SEL0 (M1SEL[0], ADDU, SUBU, SLTU, ALUOP[2]);
  or u_M3SEL (M3SEL, LB, SH, SB, LUI, LH, ORI, LW, SW);
  buf M2SEL1 (M2SEL[1], JAL);  // OR_Gate
  or M2SEL0 (M2SEL[0], LH, LW, LB);
  or BORH1 (BORH[1], SH, LH);
  or BORH0 (BORH[0], LB, SB);

  assign NPCOP[2] = 1'b0;

  // Other names for the same wires on the sheet: SLL = ALUOP[2]
endmodule

module ALUCTR (
  input  [2:0] ALUOP,
  input  [5:0] FUNC,
  output [2:0] ALUCTR
);

  wire ADDU, ADDU_out, LUI, LW, not_1_out, not_2_out, not_3_out, not_4_out, not_5_out, not_6_out, not_7_out,
       not_8_out, not_9_out, ORI, SLL_out, SLTU, SLTU_out, SUBU, SUBU_out, SW;

  not not_1 (not_1_out, FUNC[5]);
  not not_2 (not_2_out, FUNC[4]);
  not not_3 (not_3_out, FUNC[3]);
  not not_4 (not_4_out, FUNC[2]);
  not not_5 (not_5_out, FUNC[1]);
  not not_6 (not_6_out, FUNC[0]);
  and u_ADDU (ADDU_out, FUNC[5], not_2_out, not_3_out, not_4_out, not_5_out, FUNC[0]);
  and u_SUBU (SUBU_out, FUNC[5], not_2_out, not_3_out, not_4_out, FUNC[1], FUNC[0]);
  and u_SLTU (SLTU_out, FUNC[5], not_2_out, FUNC[3], not_4_out, FUNC[1], FUNC[0]);
  and SLL (SLL_out, not_1_out, not_2_out, not_3_out, not_4_out, not_5_out, not_6_out);
  or or_1 (ALUCTR[1], ORI, SLTU);
  or or_2 (ALUCTR[0], SLTU, SUBU);
  not not_7 (not_7_out, ALUOP[2]);
  not not_8 (not_8_out, ALUOP[1]);
  not not_9 (not_9_out, ALUOP[0]);
  and ADDU_2 (ADDU, not_7_out, not_8_out, not_8_out, ADDU_out, not_9_out);
  and SUBU_2 (SUBU, not_7_out, not_8_out, SUBU_out, ALUOP[0]);
  and u_ORI (ORI, not_7_out, ALUOP[1], not_9_out);
  and u_LW (LW, not_7_out, not_8_out, not_9_out);
  and u_SW (SW, not_7_out, not_8_out, not_9_out);
  and SLTU_2 (SLTU, not_7_out, ALUOP[1], SLTU_out, ALUOP[0]);
  and u_LUI (LUI, not_7_out, not_8_out, not_9_out);
  and SLL_2 (ALUCTR[2], ALUOP[2], not_8_out, SLL_out, not_9_out);

  // Other names for the same wires on the sheet: SLL = ALUCTR[2]
endmodule
