// Logisim project p3_cpu.circ as structural Verilog: 8 circuits, main circuit main
module GRF (
  input  CLK,
  input  reset,
  input  WE,
  input  [4:0] A1,
  input  [4:0] A2,
  input  [4:0] A3,
  input  [31:0] WD,
  output [31:0] RD1,
  output [31:0] RD2
);

  wire [31:0] _0, _0a, _0b, _0c, _0d, _0e, _0f, _01, _1, _01a, _01b, _01c, _01d, _01e, _01f, _02, _2, _03,
       _3, _04, _4, _05, _5, _06, _6, _07, _7, _08, _8, _09, _9, _010, _10, _011, _11, _012, _12, _013, _13,
       _014, _14, _015, _15, _016, _16, _017, _17, _018, _18, _019, _19, _20, _21, _22, _23, _24, _25, _26,
       _27, _28, _29, _30, _31;

  Register #(.width(32)) register_1 (.D({32{1'b0}}), .en(WE), .Q(_0), .clk(CLK), .clr(reset));
  Register #(.width(32)) register_2 (.D(_01), .en(WE), .Q(_1), .clk(CLK), .clr(reset));
  Register #(.width(32)) register_3 (.D(_02), .en(WE), .Q(_2), .clk(CLK), .clr(reset));
  Register #(.width(32)) register_4 (.D(_03), .en(WE), .Q(_3), .clk(CLK), .clr(reset));
  Register #(.width(32)) register_5 (.D(_04), .en(WE), .Q(_4), .clk(CLK), .clr(reset));
  Register #(.width(32)) register_6 (.D(_05), .en(WE), .Q(_5), .clk(CLK), .clr(reset));
  Register #(.width(32)) register_7 (.D(_06), .en(WE), .Q(_6), .clk(CLK), .clr(reset));
  Register #(.width(32)) register_8 (.D(_07), .en(WE), .Q(_7), .clk(CLK), .clr(reset));
  Register #(.width(32)) register_9 (.D(_08), .en(WE), .Q(_8), .clk(CLK), .clr(reset));
  Register #(.width(32)) register_10 (.D(_09), .en(WE), .Q(_9), .clk(CLK), .clr(reset));
  Register #(.width(32)) register_11 (.D(_0a), .en(WE), .Q(_10), .clk(CLK), .clr(reset));
  Register #(.width(32)) register_12 (.D(_0b), .en(WE), .Q(_11), .clk(CLK), .clr(reset));
  Register #(.width(32)) register_13 (.D(_0c), .en(WE), .Q(_12), .clk(CLK), .clr(reset));
  Register #(.width(32)) register_14 (.D(_0d), .en(WE), .Q(_13), .clk(CLK), .clr(reset));
  Register #(.width(32)) register_15 (.D(_0e), .en(WE), .Q(_14), .clk(CLK), .clr(reset));
  Register #(.width(32)) register_16 (.D(_0f), .en(WE), .Q(_15), .clk(CLK), .clr(reset));
  Register #(.width(32)) register_17 (.D(_010), .en(WE), .Q(_16), .clk(CLK), .clr(reset));
  Register #(.width(32)) register_18 (.D(_011), .en(WE), .Q(_17), .clk(CLK), .clr(reset));
  Register #(.width(32)) register_19 (.D(_012), .en(WE), .Q(_18), .clk(CLK), .clr(reset));
  Register #(.width(32)) register_20 (.D(_013), .en(WE), .Q(_19), .clk(CLK), .clr(reset));
  Register #(.width(32)) register_21 (.D(_014), .en(WE), .Q(_20), .clk(CLK), .clr(reset));
  Register #(.width(32)) register_22 (.D(_015), .en(WE), .Q(_21), .clk(CLK), .clr(reset));
  Register #(.width(32)) register_23 (.D(_016), .en(WE), .Q(_22), .clk(CLK), .clr(reset));
  Register #(.width(32)) register_24 (.D(_017), .en(WE), .Q(_23), .clk(CLK), .clr(reset));
  Register #(.width(32)) register_25 (.D(_018), .en(WE), .Q(_24), .clk(CLK), .clr(reset));
  Register #(.width(32)) register_26 (.D(_019), .en(WE), .Q(_25), .clk(CLK), .clr(reset));
  Register #(.width(32)) register_27 (.D(_01a), .en(WE), .Q(_26), .clk(CLK), .clr(reset));
  Register #(.width(32)) register_28 (.D(_01b), .en(WE), .Q(_27), .clk(CLK), .clr(reset));
  Register #(.width(32)) register_29 (.D(_01c), .en(WE), .Q(_28), .clk(CLK), .clr(reset));
  Register #(.width(32)) register_30 (.D(_01d), .en(WE), .Q(_29), .clk(CLK), .clr(reset));
  Register #(.width(32)) register_31 (.D(_01e), .en(WE), .Q(_30), .clk(CLK), .clr(reset));
  Register #(.width(32)) register_32 (.D(_01f), .en(WE), .Q(_31), .clk(CLK), .clr(reset));
  Demultiplexer #(.select(5), .width(32), .tristate("true"), .disabled(0)) demultiplexer_1 (
    .out1(_01), .out2(_02), .out3(_03), .out4(_04), .out5(_05), .out6(_06), .out7(_07), .out8(_08),
    .out9(_09), .out10(_0a), .out11(_0b), .out12(_0c), .out13(_0d), .out14(_0e), .out15(_0f), .out16(_010),
    .out17(_011), .out18(_012), .out19(_013), .out20(_014), .out21(_015), .out22(_016), .out23(_017),
    .out24(_018), .out25(_019), .out26(_01a), .out27(_01b), .out28(_01c), .out29(_01d), .out30(_01e),
    .out31(_01f), .in(WD), .sel(A3));  // open: out0, en
  Multiplexer #(.select(5), .width(32), .disabled(0)) multiplexer_1 (
    .in0(_0), .in1(_1), .in2(_2), .in3(_3), .in4(_4), .in5(_5), .in6(_6), .in7(_7), .in8(_8), .in9(_9),
    .in10(_10), .in11(_11), .in12(_12), .in13(_13), .in14(_14), .in15(_15), .in16(_16), .in17(_17),
    .in18(_18), .in19(_19), .in20(_20), .in21(_21), .in22(_22), .in23(_23), .in24(_24), .in25(_25),
    .in26(_26), .in27(_27), .in28(_28), .in29(_29), .in30(_30), .in31(_31), .out(RD1), .sel(A1));  // open: en
  Multiplexer #(.select(5), .width(32), .disabled(0)) multiplexer_2 (
    .in0(_0), .in1(_1), .in2(_2), .in3(_3), .in4(_4), .in5(_5), .in6(_6), .in7(_7), .in8(_8), .in9(_9),
    .in10(_10), .in11(_11), .in12(_12), .in13(_13), .in14(_14), .in15(_15), .in16(_16), .in17(_17),
    .in18(_18), .in19(_19), .in20(_20), .in21(_21), .in22(_22), .in23(_23), .in24(_24), .in25(_25),
    .in26(_26), .in27(_27), .in28(_28), .in29(_29), .in30(_30), .in31(_31), .out(RD2), .sel(A2));  // open: en

  // Other names for the same wires on the sheet: en = WE; r = reset
endmodule

module main (
  input  reset,
  output [31:0] out_2,
  output out_3,
  output [4:0] out_4,
  output [31:0] out_5,
  output out_6,
  output [4:0] out_7,
  output [31:0] out_8
);

  wire ALUSrc, clk, MemRead, MemtoReg, nPC_sel, RegDst, zero;
  wire [1:0] ALUOp, ExtOp;
  wire [2:0] ALUController_aluctr;
  wire [31:0] ALUResult, imm, multiplexer_3_out, RD, RD1;

  Clock clock_1 (.out(clk));
  Multiplexer #(.width(5)) multiplexer_1 (
    .in0(out_2[20:16]), .in1(out_2[25:21]), .out(out_4), .sel(RegDst));  // open: en
  Multiplexer #(.width(32)) multiplexer_2 (
    .in0({ALUResult[31:7], out_7, ALUResult[1:0]}), .in1(RD), .out(out_5), .sel(MemtoReg));  // open: en
  IFU IFU (
    .imm(imm), .clk(clk), .reset(reset), .nPC_sel(nPC_sel), .zero(zero),
    .Instr({out_2[31:16], out_2[25:21], out_2[10:0]}));
  GRF GRF (
    .CLK(clk), .reset(reset), .A1(out_2[25:21]), .A2(out_2[20:16]), .A3(out_4), .WD(out_5), .RD1(RD1),
    .RD2(out_8));  // open: WE
  Multiplexer #(.width(32)) multiplexer_3 (.in0(out_8), .in1(imm), .out(multiplexer_3_out), .sel(ALUSrc));  // open: en
  Controller controller_1 (
    .opcode(out_2[31:26]), .RegDst(RegDst), .ALUSrc(ALUSrc), .MemtoReg(MemtoReg), .nPC_sel(nPC_sel),
    .ExtOp(ExtOp), .RegWrite(out_3), .MemWrite(out_6), .MemRead(MemRead), .ALUOp(ALUOp));
  ALU ALU (
    .in1(RD1), .in2(multiplexer_3_out), .ALUctr(ALUController_aluctr), .zero(zero),
    .result({ALUResult[31:7], out_7, ALUResult[1:0]}));
  ALUController ALUController (.Func(out_2[5:0]), .ALUOp(ALUOp), .ALUctr(ALUController_aluctr));
  EXT EXT (.imm({out_2[25:21], out_2[10:0]}), .ExtOp(ExtOp), .out_3(imm));
  DM DM (.Addr(out_7), .WD(out_8), .MemWrite(out_6), .MemRead(MemRead), .clk(clk), .reset(reset), .RD(RD));

  assign out_2[15:11] = out_2[25:21];

  // Other names for the same wires on the sheet: ALUResult[6:2] = out_7; MemAddr[4:0] = out_7; Func[5:0] = out_2[5:0];
  //   imm16[15:0] = {out_2[25:21], out_2[10:0]}; Instr[31:0] = {out_2[31:16], out_2[25:21], out_2[10:0]};
  //   Shamt[4:0] = out_2[10:6]; rt[4:0] = out_2[20:16]; rd_t[4:0] = out_2[25:21]; opcode[5:0] = out_2[31:26];
  //   MemWrite = out_6; MemData[31:0] = out_8; RD2[31:0] = out_8; RegAddr[4:0] = out_4; RegData[31:0] = out_5;
  //   RegWrite = out_3
endmodule

module IFU (
  input  [31:0] imm,
  input  clk,
  input  reset,
  input  nPC_sel,
  input  zero,
  output [31:0] Instr
);

  wire and_1_out;
  wire [31:0] adder_1_out, adder_2_out, multiplexer_1_out, PC_q, shifter_1_out;

  Adder #(.width(32)) adder_1 (.a(PC_q), .b(32'h4), .out(adder_1_out));  // open: cin, cout
  Shifter #(.width(32)) shifter_1 (.in(imm), .\dist (5'b00010), .out(shifter_1_out));
  Adder #(.width(32)) adder_2 (.a(adder_1_out), .b(shifter_1_out), .out(adder_2_out));  // open: cin, cout
  and and_1 (and_1_out, nPC_sel, zero);
  Multiplexer #(.width(32)) multiplexer_1 (
    .in0(adder_1_out), .in1(adder_2_out), .out(multiplexer_1_out), .sel(and_1_out));  // open: en
  Register #(.width(32)) PC (.D(multiplexer_1_out), .Q(PC_q), .clk(clk), .clr(reset));  // open: en
  ROM #(.addrWidth(5), .dataWidth(32)) rom_1 (.addr(PC_q[6:2]), .data(Instr));  // open: sel

  // Notes on the sheet:
  //   contents of rom_1 (hex, n*v repeats v):
  //   3404007b 348501c8 3c06007b 3c07ffff 34e7ffff 868021 a48823 2249023 34080000 ad040000 ad050004
  //   ad060008 ad07000c ad100010 ad110014 ad120018 8d040000 8d05000c ad050004 ad040000 34040001 34050002
  //   34060001 10850001 10860001 ad040024 ad050028
endmodule

module Controller (
  input  [5:0] opcode,
  output [1:0] ALUOp,
  output RegDst,
  output ALUSrc,
  output MemtoReg,
  output nPC_sel,
  output RegWrite,
  output MemWrite,
  output MemRead,
  output [1:0] ExtOp
);

  wire addu_out, not_1_out, not_2_out, not_3_out, not_4_out, not_5_out, not_6_out, ori_out, subu_out;

  not not_1 (not_1_out, opcode[5]);
  not not_2 (not_2_out, opcode[2]);
  not not_3 (not_3_out, opcode[4]);
  not not_4 (not_4_out, opcode[3]);
  not not_5 (not_5_out, opcode[1]);
  not not_6 (not_6_out, opcode[0]);
  and addu (addu_out, not_1_out, not_3_out, not_4_out, not_2_out, not_5_out, not_6_out);
  and subu (subu_out, not_1_out, not_3_out, not_4_out, not_2_out, not_5_out, not_6_out);
  and ori (ori_out, opcode[0], not_5_out, opcode[2], opcode[3], not_3_out, not_1_out);
  and lw (MemRead, opcode[0], opcode[1], not_2_out, not_4_out, not_3_out, opcode[5]);
  and sw (MemWrite, opcode[0], opcode[1], not_2_out, opcode[3], not_3_out, opcode[5]);
  and beq (nPC_sel, not_6_out, not_5_out, opcode[2], not_4_out, not_3_out, not_1_out);
  and lui (ExtOp[1], opcode[0], opcode[1], opcode[2], opcode[3], not_3_out, not_1_out);
  or or_1 (RegDst, addu_out, subu_out);
  or or_2 (ALUSrc, ori_out, MemRead, MemWrite, ExtOp[1]);
  or or_3 (ExtOp[0], MemRead, MemWrite);
  or or_4 (RegWrite, addu_out, subu_out, ori_out, ori_out, ExtOp[1]);
  or or_5 (ALUOp[1], addu_out, ori_out, subu_out);
  or or_6 (ALUOp[0], ori_out, nPC_sel);

  assign MemtoReg = MemRead;
endmodule

module EXT (
  input  [15:0] imm,
  input  [1:0] ExtOp,
  output [31:0] out_3
);

  wire [31:0] bit_extender_1_out, bit_extender_2_out;

  assign bit_extender_1_out = {{16{1'b0}}, imm};  // Bit_Extender bit_extender_1
  assign bit_extender_2_out = {{16{imm[15]}}, imm};  // Bit_Extender bit_extender_2
  Multiplexer #(.select(2), .width(32)) multiplexer_1 (
    .in0(bit_extender_1_out), .in1(bit_extender_2_out), .in2({imm, {16{1'b0}}}), .out(out_3), .sel(ExtOp));  // open: in3, en
endmodule

module ALUController (
  input  [5:0] Func,
  input  [1:0] ALUOp,
  output [2:0] ALUctr
);

  wire addu_out, beq_out, lui_out, lw_sw_out, not_1_out, not_2_out, not_3_out, not_4_out, not_5_out,
       not_6_out, not_7_out, not_8_out, subu_out;

  not not_1 (not_1_out, Func[0]);
  not not_2 (not_2_out, Func[1]);
  not not_3 (not_3_out, Func[2]);
  not not_4 (not_4_out, Func[3]);
  not not_5 (not_5_out, Func[4]);
  not not_6 (not_6_out, Func[5]);
  not not_7 (not_7_out, ALUOp[0]);
  not not_8 (not_8_out, ALUOp[1]);
  and lw_sw (lw_sw_out, not_8_out, not_7_out);
  and beq (beq_out, not_8_out, ALUOp[0]);
  and addu (addu_out, ALUOp[1], not_7_out, Func[5], not_5_out, not_4_out, not_3_out, not_2_out, not_1_out);
  and subu (subu_out, ALUOp[1], not_7_out, Func[5], not_5_out, not_4_out, not_3_out, Func[1], not_1_out);
  and lui (lui_out, not_8_out, not_7_out);
  and ori (ALUctr[0], ALUOp[1], ALUOp[0]);
  or or_1 (ALUctr[1], lw_sw_out, addu_out, lui_out);
  or or_2 (ALUctr[2], beq_out, subu_out);
endmodule

module ALU (
  input  [31:0] in1,
  input  [31:0] in2,
  input  [2:0] ALUctr,
  output zero,
  output [31:0] result
);

  wire [31:0] add, \and , \or , sub;

  Adder #(.width(32)) adder_1 (.a(in1), .b(in2), .out(add));  // open: cin, cout
  Subtractor #(.width(32)) subtractor_1 (.a(in1), .b(in2), .out(sub));  // open: bin, bout
  Comparator #(.width(32)) comparator_1 (.a(in1), .b(in2), .eq(zero));  // open: gt, lt
  assign \or  = in1 | in2;  // OR_Gate or_1, 32 bits wide
  assign \and  = in2 & in1;  // AND_Gate and_1, 32 bits wide
  Multiplexer #(.select(3), .width(32)) multiplexer_1 (
    .in0(\and ), .in1(\or ), .in2(add), .in4(sub), .out(result), .sel(ALUctr));  // open: in3, in5, in6, in7, en
endmodule

module DM (
  input  [4:0] Addr,
  input  [31:0] WD,
  input  MemWrite,
  input  MemRead,
  input  clk,
  input  reset,
  output [31:0] RD
);

  RAM #(.addrWidth(5), .dataWidth(32), .bus("separate")) ram_1 (
    .addr(Addr), .din(WD), .data(RD), .str(MemWrite), .sel(1'b1), .clk(clk), .ld(MemRead), .clr(reset));
endmodule
